// Logisim project 4bit-ALU.circ as structural Verilog
module logic_unit (
  input  Ao,
  input  A1,
  input  A2,
  input  A3,
  input  Bo,
  input  B1,
  input  B2,
  input  B3
);

  wire arithmetic_unit_1_out_6, arithmetic_unit_1_out_7, arithmetic_unit_1_out_8, arithmetic_unit_1_out_9,
       n7404_1_p6, n7404_1_p8, n7404_1_p10, n7404_1_p12, n7408_1_p13, n7408_1_p14, n74157_1_p3, n74157_1_p6,
       n74157_1_p7, n74157_1_p9, n74157_1_p10, n74157_1_p12, n74157_2_p3, n74157_2_p6, n74157_2_p9,
       n74157_2_p12;

  // _7404 7404_1: pin names not known; wires that end beside it: Bo, B1, B2, B3, Ao, n7404_1_p6, A1, n7404_1_p8, A3, n7404_1_p10, A2, n7404_1_p12
  // _7408 7408_1: pin names not known; wires that end beside it: Bo, B1, B2, B3, Ao, Bo, A1, B1, A2, B2, A3, B3, n7408_1_p13, n7408_1_p14
  arithmetic_unit arithmetic_unit_1 (
    .out_6(arithmetic_unit_1_out_6), .out_7(arithmetic_unit_1_out_7), .out_8(arithmetic_unit_1_out_8),
    .out_9(arithmetic_unit_1_out_9));  // open: in_1, in_2, in_3, in_4, out_5
  // _74157 74157_1: pin names not known; wires that end beside it: n7408_1_p14, n7404_1_p6, n74157_1_p3, n7408_1_p13, n7404_1_p8, n74157_1_p6, n74157_1_p7, n7404_1_p10, n74157_1_p9, n74157_1_p10, n7404_1_p12, n74157_1_p12, n74157_1_p7, n74157_1_p10
  // _74157 74157_2: pin names not known; wires that end beside it: arithmetic_unit_1_out_6, n74157_1_p3, n74157_2_p3, n74157_1_p6, arithmetic_unit_1_out_7, n74157_2_p6, n74157_1_p9, arithmetic_unit_1_out_9, n74157_2_p9, n74157_1_p12, arithmetic_unit_1_out_8, n74157_2_p12, n74157_2_p3, n74157_2_p6, n74157_2_p9, n74157_2_p12
endmodule

module arithmetic_unit (
  input  in_1,
  input  in_2,
  input  in_3,
  input  in_4,
  output out_5,
  output out_6,
  output out_7,
  output out_8,
  output out_9
);
endmodule

module \logic  (
  input  Ao,
  input  A1,
  input  A2,
  input  A3,
  input  in_5,
  input  Bo,
  input  B1,
  input  B2,
  input  B3
);

  wire n7404_1_p2, n7404_1_p4, n7404_1_p6, n7404_1_p8, n7404_1_p9, n7404_1_p10, n7404_1_p11, n7404_1_p12,
       n74157_1_p3, n74157_1_p6, n74157_1_p8, n74157_1_p11;

  // _7404 7404_1: pin names not known; wires that end beside it: Ao, n7404_1_p2, A1, n7404_1_p4, A2, n7404_1_p6, A3, n7404_1_p8, n7404_1_p9, n7404_1_p10, n7404_1_p11, n7404_1_p12
  // _74157 74157_1: pin names not known; wires that end beside it: in_5, n7404_1_p2, n74157_1_p3, n7404_1_p9, n7404_1_p4, n74157_1_p6, n7404_1_p10, n74157_1_p8, n7404_1_p6, n7404_1_p11, n74157_1_p11, n7404_1_p8, n7404_1_p12
  // _7408 7408_1: pin names not known; wires that end beside it: Ao, Bo, n74157_1_p3, A1, B1, n74157_1_p6, A2, B2, n74157_1_p8, A3, B3, n74157_1_p11, n7404_1_p9, n7404_1_p10, n7404_1_p11, n7404_1_p12

  // Notes on the sheet:
  //   s2's1's0'
  //   F1
  //   F0
  //   F2
  //   F3
endmodule
