// Logisim project ALU.circ as structural Verilog: 8 circuits, main circuit main
module main (
  input  B3,
  input  B2,
  input  B1,
  input  B0,
  input  A3,
  input  A2,
  input  A1,
  input  A0,
  input  CS2,
  input  CS1,
  input  CS0,
  output C,
  output V,
  output Z,
  output S,
  output F4,
  output F3,
  output F2,
  output F1
);

  ALU alu_1 (
    .CS2(CS2), .CS1(CS1), .CS0(CS0), .B3(B3), .B2(B2), .B1(B1), .B0(B0), .A3(A3), .A2(A2), .A1(A1), .A0(A0),
    .F4(F4), .F3(F3), .F2(F2), .F1(F1), .C(C), .V(V), .Z(Z), .S(S));

  // Notes on the sheet:
  //   CS2
  //   CS1
  //   0
  //   0
  //   0
  //   0
  //   1
  //   0
  //   1
  //   0
  //   0
  //   1
  //   1
  //   0
  //   1
  //   1
  //   1
  //   1
  //   CS0
  //   0
  //   1
  //   0
  //   1
  //   0
  //   1
  //   0
  //   1
  //   A.B
  //   A--
  //   A-B
  //   ~A
  //   Trans A
  //   Trans A
  //   A-B
  //   A+B
endmodule

// 4 Bit ALU
module ALU (
  input  CS2,
  input  CS1,
  input  CS0,
  input  B3,
  input  B2,
  input  B1,
  input  B0,
  input  A3,
  input  A2,
  input  A1,
  input  A0,
  output C,
  output V,
  output Z,
  output S,
  output F4,
  output F3,
  output F2,
  output F1
);

  wire adder_1_c3, adder_1_s0, adder_1_s1, adder_1_s2, adder_1_s3, arith_1_y0, arith_1_y1, arith_1_y2,
       arith_1_y3, decoder_2_1__000, decoder_2_1__001, decoder_2_1__010, decoder_2_1__011, decoder_2_1__110,
       decoder_2_1__111, n7400_1_p3, n7400_1_p6, n7400_1_p11, n7400_1_p14, n7404_1_p2, n7404_1_p4,
       n7404_1_p6, n7404_1_p10, n7404_1_p12, n7404_1_p13, n7432_1_p7, n7432_1_p9, n74157_1_p3, n74157_1_p4,
       n74157_1_p6, n74157_1_p7, n74157_1_p12, n74157_1_p13, n74157_1_p15, n74157_1_p16;

  Decoder_2 decoder_2_1 (
    .S0(CS0), .S1(CS1), .S2(CS2), ._000(decoder_2_1__000), ._001(decoder_2_1__001), ._010(decoder_2_1__010),
    ._011(decoder_2_1__011), ._110(decoder_2_1__110), ._111(decoder_2_1__111));  // open: _100, _101
  // _7400 7400_1: pin names not known; wires that end beside it: decoder_2_1__011, decoder_2_1__000, n7400_1_p3, decoder_2_1__000, decoder_2_1__000, n7400_1_p6, 1'b0, 1'b1, decoder_2_1__110, decoder_2_1__010, n7400_1_p11, decoder_2_1__001, decoder_2_1__111, n7400_1_p14, decoder_2_1__000, decoder_2_1__001, decoder_2_1__010, decoder_2_1__011, decoder_2_1__110
  // _7404 7404_1: pin names not known; wires that end beside it: A0, n7404_1_p2, A1, n7404_1_p4, n7400_1_p14, n7404_1_p6, 1'b0, 1'b1, A2, n7404_1_p10, A3, n7404_1_p12, n7404_1_p13, Z, A3, A2, A1, A0
  // _74157 74157_1: pin names not known; wires that end beside it: n7400_1_p6, n7404_1_p2, n74157_1_p3, n74157_1_p4, n7404_1_p4, n74157_1_p6, n74157_1_p7, 1'b0, 1'b1, 1'b0, n7404_1_p10, n74157_1_p12, n74157_1_p13, n7404_1_p12, n74157_1_p15, n74157_1_p16
  // _7408 7408_1: pin names not known; wires that end beside it: A0, B0, n74157_1_p3, A1, B1, n74157_1_p6, 1'b0, 1'b1, A2, B2, n74157_1_p12, A3, B3, n74157_1_p15, A0, A1, A2, A3, B0, B1, B2, B3
  Arith arith_1 (
    .B3(B3), .B2(B2), .B1(B1), .B0(B0), .D1_prime_D7_prime(n7404_1_p6), .CS1(CS1), .Y3(arith_1_y3),
    .Y2(arith_1_y2), .Y1(arith_1_y1), .Y0(arith_1_y0));
  Adder adder_1 (
    .B3(arith_1_y3), .B2(arith_1_y2), .B1(arith_1_y1), .B0(arith_1_y0), .A3(A3), .A2(A2), .A1(A1), .A0(A0),
    .C4(C), .S3(adder_1_s3), .C3(adder_1_c3), .S2(adder_1_s2), .S1(adder_1_s1), .S0(adder_1_s0),
    .Cin(n7400_1_p11));  // open: C2, C1
  // _74157 74157_2: pin names not known; wires that end beside it: n7400_1_p3, adder_1_s0, n74157_1_p4, F1, adder_1_s1, n74157_1_p7, F2, 1'b0, 1'b1, 1'b0, adder_1_s2, n74157_1_p13, F3, adder_1_s3, n74157_1_p16, F4, adder_1_s2, adder_1_s3
  // _7486 7486_1: pin names not known; wires that end beside it: adder_1_s0, adder_1_s1, C, adder_1_c3, V, 1'b0, 1'b1, 1'b1
  // _7432 7432_1: pin names not known; wires that end beside it: n74157_1_p16, n74157_1_p13, n74157_1_p7, n74157_1_p4, F1, F2, n7432_1_p7, n7432_1_p7, n7432_1_p9, n7404_1_p13, 1'b0, 1'b1, F3, F4, n7432_1_p9

  assign S = F4;

  // Notes on the sheet:
  //   Cin = CS1*CS0'
  //   Logic Unit
  //   Arithmetic Unit
  //   MUX
  //   NOT
  //   AND
  //   Bi to Yi
  //   S0
  //   S1
  //   S2
  //   S3
  //   MUX
  //   Overflow
endmodule

module Decoder (
  input  S0,
  input  S1,
  input  S2,
  output _000,
  output _001,
  output _010,
  output _011,
  output _100,
  output _101,
  output _110,
  output _111
);

  wire n74138_1_p7, n74138_1_p10, n74138_1_p11, n74138_1_p12, n74138_1_p13, n74138_1_p14;

  // _74138 74138_1: pin names not known; wires that end beside it: S0, S1, S2, 1'b0, 1'b0, 1'b1, n74138_1_p7, 1'b0, 1'b1, n74138_1_p10, n74138_1_p11, n74138_1_p12, n74138_1_p13, n74138_1_p14
  // _7404 7404_1: pin names not known; wires that end beside it: n74138_1_p11, _001, n74138_1_p12, _010, n74138_1_p13, _011, 1'b0, 1'b1, n74138_1_p10, _000, n74138_1_p7, _111, n74138_1_p14, _110, _100, _101

  // Notes on the sheet:
  //   3x8 DECODER
endmodule

module Adder (
  input  B3,
  input  B2,
  input  B1,
  input  B0,
  input  A3,
  input  A2,
  input  A1,
  input  A0,
  input  Cin,
  output S3,
  output S2,
  output S1,
  output S0,
  output C4,
  output C3,
  output C2,
  output C1
);

  // _7483 7483_1: pin names not known; wires that end beside it: A1, C1, C1, 1'b1, C1, 1'b0, 1'b0, B1, S1, C2, Cin, 1'b0, B0, A0, S0
  // _7483 7483_2: pin names not known; wires that end beside it: A3, C3, C3, 1'b1, C3, 1'b0, 1'b0, B3, S3, C4, C2, 1'b0, B2, A2, S2
endmodule

// Y
module Arithmetic (
  input  B3,
  input  B2,
  input  B1,
  input  B0,
  input  CS2CS1CS0,
  input  CS2_prime_CS1_prime_CS0,
  input  Cin,
  output Y3,
  output Y2,
  output Y1,
  output Y0
);

  wire n7404_1_p2, n7404_1_p4, n7404_1_p8, n7404_1_p10, n7408_1_p1, n7408_1_p2, n7408_1_p3, n7408_1_p4,
       n7408_1_p5, n7408_1_p6, n7408_1_p7, n7408_1_p8, n7432_1_p3, n7432_1_p6, n7432_1_p11, n7432_1_p14;

  // _7408 7408_1: pin names not known; wires that end beside it: n7408_1_p1, n7408_1_p2, n7408_1_p3, n7408_1_p4, n7408_1_p5, n7408_1_p6, n7408_1_p7, n7408_1_p8, B1, CS2CS1CS0, n7408_1_p4, B0, CS2CS1CS0, n7408_1_p3, 1'b0, 1'b1, B2, CS2CS1CS0, n7408_1_p2, B3, CS2CS1CS0, n7408_1_p1
  // _7432 7432_1: pin names not known; wires that end beside it: n7408_1_p8, n7408_1_p4, n7432_1_p3, n7408_1_p7, n7408_1_p3, n7432_1_p6, 1'b0, 1'b1, n7408_1_p6, n7408_1_p2, n7432_1_p11, n7408_1_p5, n7408_1_p1, n7432_1_p14
  // _7432 7432_2: pin names not known; wires that end beside it: CS2_prime_CS1_prime_CS0, n7432_1_p3, Y0, CS2_prime_CS1_prime_CS0, n7432_1_p6, Y1, 1'b0, 1'b1, n7432_1_p11, CS2_prime_CS1_prime_CS0, Y2, n7432_1_p14, CS2_prime_CS1_prime_CS0, Y3
  // _7404 7404_1: pin names not known; wires that end beside it: B0, n7404_1_p2, B1, n7404_1_p4, 1'b0, 1'b1, B2, n7404_1_p8, B3, n7404_1_p10, B3, B2, B1, B0
  // _7408 7408_2: pin names not known; wires that end beside it: n7404_1_p2, Cin, n7408_1_p8, n7404_1_p4, Cin, n7408_1_p7, 1'b0, 1'b1, n7404_1_p8, Cin, n7408_1_p6, n7404_1_p10, Cin, n7408_1_p5, n7408_1_p1, n7408_1_p2, n7408_1_p3, n7408_1_p4, n7408_1_p5, n7408_1_p6, n7408_1_p7

  // Notes on the sheet:
  //   Yi = CS2'.CS1'.CS0 + Cin.Bi' + CS2.CS1.CS0.Bi 
  //   111
  //   001
  //   CS2.CS1.CS0.B3
  //   CS2.CS1.CS0.B2
  //   CS2.CS1.CS0.B1
  //   CS2.CS1.CS0.B0
  //   Cin.B3
  //   Cin.B2
  //   Cin.B1
  //   Cin.B0
  //   010
  //   110
  //   111
  //   CS2*CS1*CS0*Bi
  //   B1'
  //   B0'
  //   B2'
  //   B3
  //   B2
  //   B1
  //   B0
  //   B3'
  //   Bi' CS1 CS0'
endmodule

module LU (
);

  // _74157 74157_1: pin names not known
  // _7400 7400_1: pin names not known
endmodule

// Decoder
module Decoder_2 (
  input  S0,
  input  S1,
  input  S2,
  output _000,
  output _001,
  output _010,
  output _011,
  output _100,
  output _101,
  output _110,
  output _111
);

  // _74138 74138_1: pin names not known; wires that end beside it: S0, S1, S2, 1'b0, 1'b0, 1'b1, _111, 1'b0, 1'b1, _000, _001, _010, _011, _110

  // Notes on the sheet:
  //   3x8 DECODER
endmodule

// Y
module Arith (
  input  B3,
  input  B2,
  input  B1,
  input  B0,
  input  D1_prime_D7_prime,
  input  CS1,
  output Y3,
  output Y2,
  output Y1,
  output Y0
);

  wire n7486_1_p14, n74157_1_p5, n74157_1_p8, n74157_1_p13;

  // _74157 74157_1: pin names not known; wires that end beside it: 1'b1, CS1, 1'b1, B0, n74157_1_p5, 1'b1, B1, n74157_1_p8, 1'b1, 1'b0, 1'b1, B2, n74157_1_p13, 1'b1, B2, B3, B2, B1, B0
  // _7486 7486_1: pin names not known; wires that end beside it: 1'b0, Y3, Y2, Y1, Y0, 1'b0, n74157_1_p5, D1_prime_D7_prime, Y0, n74157_1_p8, D1_prime_D7_prime, Y1, 1'b0, n7486_1_p14, 1'b1, D1_prime_D7_prime, n74157_1_p13, Y2, D1_prime_D7_prime, n7486_1_p14, Y3, D1_prime_D7_prime
endmodule
