// Logisim project B1_Group1.circ as structural Verilog: 9 circuits, main circuit main
module main (
  input  B3,
  input  B2,
  input  B1,
  input  B0,
  input  A3,
  input  A2,
  input  A1,
  input  A0,
  input  CS2,
  input  CS1,
  input  CS0,
  output C,
  output V,
  output Z,
  output S,
  output F4,
  output F3,
  output F2,
  output F1
);

  ALU_Flag alu_flag_1 (
    .CS2(CS2), .CS1(CS1), .CS0(CS0), .B3(B3), .B2(B2), .B1(B1), .B0(B0), .A3(A3), .A2(A2), .A1(A1), .A0(A0),
    .F3(F4), .F2(F3), .F1(F2), .F0(F1), .C(C), .V(V), .Z(Z), .S(S));

  // Notes on the sheet:
  //   CS2
  //   CS1
  //   0
  //   0
  //   0
  //   0
  //   1
  //   0
  //   1
  //   0
  //   0
  //   1
  //   1
  //   0
  //   1
  //   1
  //   1
  //   1
  //   CS0
  //   0
  //   1
  //   0
  //   1
  //   0
  //   1
  //   0
  //   1
  //   A.B
  //   A--
  //   A-B
  //   ~A
  //   Trans A
  //   Trans A
  //   A-B
  //   A+B
endmodule

// 4 Bit ALU
module ALU_Flag (
  input  CS2,
  input  CS1,
  input  CS0,
  input  B3,
  input  B2,
  input  B1,
  input  B0,
  input  A3,
  input  A2,
  input  A1,
  input  A0,
  output C,
  output V,
  output Z,
  output S,
  output F3,
  output F2,
  output F1,
  output F0
);

  wire alu_1_cout, alu_1_f0, alu_1_f1, alu_1_f2, alu_1_f3, alu_1_y3, selection_bits_1_cs1_2,
       selection_bits_1_d0_d3, selection_bits_1_d1_d7, selection_bits_1_d1_prime_d7_prime,
       selection_bits_1_d2_d6;

  Selection_Bits selection_bits_1 (
    .CS2(CS2), .CS1(CS1), .CS0(CS0), .D2_D6(selection_bits_1_d2_d6), .D0_D3(selection_bits_1_d0_d3),
    .D1_prime_D7_prime(selection_bits_1_d1_prime_d7_prime), .CS1_2(selection_bits_1_cs1_2),
    .D1_D7(selection_bits_1_d1_d7));
  ALU alu_1 (
    .A0(A0), .A1(A1), .A2(A2), .A3(A3), .B0(B0), .B1(B1), .B2(B2), .B3(B3), .Cin(selection_bits_1_d2_d6),
    .D0_D3(selection_bits_1_d0_d3), .D1_prime_D7_prime(selection_bits_1_d1_prime_d7_prime),
    .CS1(selection_bits_1_cs1_2), .Y3(alu_1_y3), .Cout(alu_1_cout), .F0(alu_1_f0), .F1(alu_1_f1),
    .F2(alu_1_f2), .F3(alu_1_f3));
  Flag_Generator flag_generator_1 (
    .X3(A3), .Y3(alu_1_y3), .Cout(alu_1_cout), .F0(alu_1_f0), .F1(alu_1_f1), .F2(alu_1_f2), .F3(alu_1_f3),
    .CS1(selection_bits_1_cs1_2), .D1_D7(selection_bits_1_d1_d7), .F3_2(F3), .F2_2(F2), .F1_2(F1), .F0_2(F0),
    .C(C), .V(V), .Z(Z), .S(S));

  // Notes on the sheet:
  //   Selection Bit
  //   4 bit operands
  //   Providing required
  //   terms and input
  //   to Main ALU
endmodule

// LU
module Logical_Unit (
  input  CS1,
  input  A0,
  input  A1,
  input  A2,
  input  A3,
  input  B0,
  input  B1,
  input  B2,
  input  B3,
  output F0,
  output F1,
  output F2,
  output F3
);

  wire n7400_1_p3, n7400_1_p6, n7400_1_p11, n7400_1_p14;

  _74158 u_74158_1 (
    .S(CS1), .A0(n7400_1_p3), .A1(n7400_1_p6), .A2(n7400_1_p11), .A3(n7400_1_p14), .B0(A0), .B1(A1), .B2(A2),
    .B3(A3), .Y0_prime(F0), .Y1_prime(F1), .Y2_prime(F2), .Y3_prime(F3));
  // _7400 7400_1: pin names not known; wires that end beside it: A0, B0, n7400_1_p3, A1, B1, n7400_1_p6, 1'b0, 1'b1, A2, B2, n7400_1_p11, A3, B3, n7400_1_p14
endmodule

// Y
module Y_Generator (
  input  B0,
  input  B1,
  input  B2,
  input  B3,
  input  D1_prime_D7_prime,
  input  CS1,
  output Y0,
  output Y1,
  output Y2,
  output Y3
);

  wire n7486_1_p14, n74157_1_p5, n74157_1_p8, n74157_1_p13;

  // _74157 74157_1: pin names not known; wires that end beside it: 1'b1, CS1, 1'b1, B0, n74157_1_p5, 1'b1, B1, n74157_1_p8, 1'b1, 1'b0, 1'b1, B2, n74157_1_p13, 1'b1, B3, B0, B1, B2, B3
  // _7486 7486_1: pin names not known; wires that end beside it: 1'b0, Y0, Y1, Y2, Y3, 1'b0, n74157_1_p5, D1_prime_D7_prime, Y0, n74157_1_p8, D1_prime_D7_prime, Y1, 1'b0, n7486_1_p14, 1'b1, D1_prime_D7_prime, n74157_1_p13, Y2, D1_prime_D7_prime, n7486_1_p14, Y3, D1_prime_D7_prime

  // Notes on the sheet:
  //   Bi to Yi
endmodule

// AU
module Arithmetic_Unit (
  input  Cin,
  input  A0,
  input  A1,
  input  A2,
  input  A3,
  input  B0,
  input  B1,
  input  B2,
  input  B3,
  input  D1_prime_D7_prime,
  input  CS1,
  output Y3,
  output Cout,
  output S0,
  output S1,
  output S2,
  output S3
);

  wire y_generator_1_y0, y_generator_1_y1, y_generator_1_y2;

  Y_Generator y_generator_1 (
    .B0(B0), .B1(B1), .B2(B2), .B3(B3), .D1_prime_D7_prime(D1_prime_D7_prime), .CS1(CS1),
    .Y0(y_generator_1_y0), .Y1(y_generator_1_y1), .Y2(y_generator_1_y2), .Y3(Y3));
  // _7483 7483_1: pin names not known; wires that end beside it: S0, S1, S2, S3, A3, S2, A2, y_generator_1_y2, 1'b1, S1, y_generator_1_y1, A1, Y3, S3, Cout, Cin, 1'b0, y_generator_1_y0, A0, S0, A0, A1, A2, A3, y_generator_1_y0, y_generator_1_y1, y_generator_1_y2

  // Notes on the sheet:
  //   Arithmetic Unit
  //   Bi to Yi
  //   S0
  //   S1
  //   S2
  //   S3
endmodule

// 4-ALU
module ALU (
  input  Cin,
  input  D0_D3,
  input  D1_prime_D7_prime,
  input  CS1,
  input  A0,
  input  A1,
  input  A2,
  input  A3,
  input  B0,
  input  B1,
  input  B2,
  input  B3,
  output Y3,
  output Cout,
  output F0,
  output F1,
  output F2,
  output F3
);

  wire arithmetic_unit_1_s0, arithmetic_unit_1_s1, arithmetic_unit_1_s2, arithmetic_unit_1_s3,
       logical_unit_1_f0, logical_unit_1_f1, logical_unit_1_f2, logical_unit_1_f3;

  Arithmetic_Unit arithmetic_unit_1 (
    .Cin(Cin), .A0(A0), .A1(A1), .A2(A2), .A3(A3), .B0(B0), .B1(B1), .B2(B2), .B3(B3),
    .D1_prime_D7_prime(D1_prime_D7_prime), .CS1(CS1), .Y3(Y3), .Cout(Cout), .S0(arithmetic_unit_1_s0),
    .S1(arithmetic_unit_1_s1), .S2(arithmetic_unit_1_s2), .S3(arithmetic_unit_1_s3));
  Logical_Unit logical_unit_1 (
    .CS1(CS1), .A0(A0), .A1(A1), .A2(A2), .A3(A3), .B0(B0), .B1(B1), .B2(B2), .B3(B3),
    .F0(logical_unit_1_f0), .F1(logical_unit_1_f1), .F2(logical_unit_1_f2), .F3(logical_unit_1_f3));
  // _74157 74157_1: pin names not known; wires that end beside it: F0, F1, F2, F3, D0_D3, arithmetic_unit_1_s0, logical_unit_1_f0, F0, arithmetic_unit_1_s1, logical_unit_1_f1, F1, 1'b0, 1'b1, 1'b0, arithmetic_unit_1_s2, logical_unit_1_f2, F2, arithmetic_unit_1_s3, logical_unit_1_f3, F3, 1'b1, logical_unit_1_f0, logical_unit_1_f1, logical_unit_1_f2, arithmetic_unit_1_s0, arithmetic_unit_1_s1, arithmetic_unit_1_s2, arithmetic_unit_1_s3

  // Notes on the sheet:
  //   Logic Unit
  //   Arithmetic Unit
  //   Merge two units
endmodule

// FLAG
module Flag_Generator (
  input  X3,
  input  Y3,
  input  Cout,
  input  F0,
  input  F1,
  input  F2,
  input  F3,
  input  CS1,
  input  D1_D7,
  output C,
  output V,
  output Z,
  output S,
  output F3_2,
  output F2_2,
  output F1_2,
  output F0_2
);

  wire n7408_1_p3, n7408_1_p4, n7432_1_p3, n7432_1_p5, n7486_1_p1, n7486_1_p4, n7486_1_p10;

  // _7408 7408_1: pin names not known; wires that end beside it: 1'b0, 1'b1, n7408_1_p3, n7408_1_p4, V, Cout, n7408_1_p3, C
  // _7486 7486_1: pin names not known; wires that end beside it: n7486_1_p1, Y3, n7408_1_p4, n7486_1_p4, 1'b1, Z, 1'b0, 1'b1, X3, n7486_1_p10, n7486_1_p1, F3, Cout, n7486_1_p10
  // _7432 7432_1: pin names not known; wires that end beside it: F0, F1, n7432_1_p3, n7432_1_p3, n7432_1_p5, n7486_1_p4, 1'b0, 1'b1, F2, F3, n7432_1_p5, CS1, D1_D7, n7408_1_p3

  assign F0_2 = F0;
  assign F1_2 = F1;
  assign F2_2 = F2;
  assign F3_2 = F3;
  assign S = F3;

  // Notes on the sheet:
  //   MUX
  //   Finding NOR of all
  //   output to set
  //   Zero flag
  //   C_3 = S_4 XOR A_4 XOR B_4
  //   V = C_3 XOR C_OUT
  //   Overflow
endmodule

// SB
module Selection_Bits (
  input  CS2,
  input  CS1,
  input  CS0,
  output D2_D6,
  output D0_D3,
  output D1_prime_D7_prime,
  output CS1_2,
  output D1_D7
);

  wire n74138_1_p7, n74138_1_p10, n74138_1_p11, n74138_1_p12, n74138_1_p13, n74138_1_p14;

  // _74138 74138_1: pin names not known; wires that end beside it: CS0, CS1, CS2, 1'b0, 1'b0, 1'b1, n74138_1_p7, 1'b0, 1'b1, n74138_1_p10, n74138_1_p11, n74138_1_p12, n74138_1_p13, n74138_1_p14
  // _7400 7400_1: pin names not known; wires that end beside it: n74138_1_p13, n74138_1_p10, D0_D3, D1_D7, D1_D7, D1_prime_D7_prime, 1'b0, 1'b1, n74138_1_p14, n74138_1_p12, D2_D6, n74138_1_p11, n74138_1_p7, D1_D7, n74138_1_p13, n74138_1_p14

  assign CS1_2 = CS1;

  // Notes on the sheet:
  //   Generating all
  //   required terms
  //   using decoder
  //   1. D2+D6 
  //   2. D1'.D7'
  //   3. D0+D3
endmodule

module _74158 (
  input  S,
  input  A0,
  input  A1,
  input  A2,
  input  A3,
  input  B0,
  input  B1,
  input  B2,
  input  B3,
  output Y0_prime,
  output Y1_prime,
  output Y2_prime,
  output Y3_prime
);

  wire n74157_1_p4, n74157_1_p7, n74157_1_p13, n74157_1_p16;

  // _74157 74157_1: pin names not known; wires that end beside it: S, A0, B0, n74157_1_p4, A1, B1, n74157_1_p7, 1'b0, 1'b1, 1'b0, A2, B2, n74157_1_p13, A3, B3, n74157_1_p16
  // _7404 7404_1: pin names not known; wires that end beside it: n74157_1_p4, Y0_prime, n74157_1_p7, Y1_prime, n74157_1_p13, Y2_prime, n74157_1_p16, Y3_prime
endmodule
