// Logisim project 2.circ as structural Verilog: 5 circuits, main circuit main_2
module main_2 (
  input  [31:0] B,
  input  [31:0] A,
  output result_sign,
  output [9:0] result_exp,
  output [20:0] result_frac,
  output overflow,
  output underflow
);

  wire bit_extender_6_out, bitfinder_3_found, comparator_1_gt, comparator_2_gt, comparator_3_eq,
       final_adder_2_1_overflow, final_adder_2_1_underflow, multiplexer_1_out, multiplexer_2_out,
       n7404_1_pin12, n7432_1_pin5, n7432_1_pin6, n7432_1_pin9, rounding_2_1_out_5;
  wire [4:0] bit_extender_1_out;
  wire [5:0] normalizer_2_1_difference, normalizer_after_rounding_2_1_difference;
  wire [9:0] multiplexer_5_out, multiplexer_6_out, multiplexer_8_out, subtractor_1_out;
  wire [10:0] bit_extender_5_out, final_adder_2_1_exponent, final_adder_2_2_exponent, multiplexer_11_out;
  wire [21:0] multiplexer_7_out, multiplexer_9_out;
  wire [21:21] bitfinder_1_found, bitfinder_2_found;
  wire [22:0] adder_2_out, bit_extender_7_out, normalizer_after_rounding_2_1_result;
  wire [30:0] adder_1_out, bit_extender_3_out, normalizer_2_1_result;
  wire [31:0] bit_extender_2_out, bit_extender_4_out, multiplexer_3_out, multiplexer_4_out,
       multiplexer_10_out, negator_1_out, negator_2_out, negator_3_out, shifter_1_out, shifter_2_out,
       shifter_3_out;

  // Probe on multiplexer_3_out
  Multiplexer multiplexer_1 (.in0(B[31]), .in1(A[31]), .out(multiplexer_1_out), .sel(comparator_1_gt));
  Negator #(.width(32)) negator_1 (.in(shifter_3_out), .out(negator_1_out));
  Negator #(.width(32)) negator_2 (.in(shifter_2_out), .out(negator_2_out));
  Multiplexer multiplexer_2 (.in0(A[31]), .in1(B[31]), .out(multiplexer_2_out), .sel(comparator_1_gt));
  Multiplexer #(.width(32)) multiplexer_3 (
    .in0(shifter_3_out), .in1(negator_1_out), .out(multiplexer_3_out), .sel(multiplexer_1_out));
  // Probe on multiplexer_3_out
  Multiplexer #(.width(32)) multiplexer_4 (
    .in0(shifter_2_out), .in1(negator_2_out), .out(multiplexer_4_out), .sel(multiplexer_2_out));
  // Probe on multiplexer_4_out
  BitFinder #(.width(31)) bitfinder_1 (.in(A[30:0]), .found(bitfinder_1_found[21]));  // open: index
  // Probe on A[30:21]
  Comparator #(.mode("unsigned"), .width(10)) comparator_1 (
    .a(A[30:21]), .b(B[30:21]), .gt(comparator_1_gt));  // open: eq, lt
  Multiplexer #(.width(10)) multiplexer_5 (
    .in0(B[30:21]), .in1(A[30:21]), .out(multiplexer_5_out), .sel(comparator_1_gt));
  // Probe on multiplexer_4_out
  // Probe on {bitfinder_1_found[21], A[20:0]}
  Multiplexer #(.width(10)) multiplexer_6 (
    .in0(A[30:21]), .in1(B[30:21]), .out(multiplexer_6_out), .sel(comparator_1_gt));
  // Probe on subtractor_1_out
  Subtractor #(.width(10)) subtractor_1 (
    .a(multiplexer_5_out), .b(multiplexer_6_out), .out(subtractor_1_out));  // open: bin, bout
  Comparator #(.mode("unsigned"), .width(10)) comparator_2 (
    .a(subtractor_1_out), .b(10'h1f), .gt(comparator_2_gt));  // open: eq, lt
  // Probe on B[30:21]
  Multiplexer #(.width(22)) multiplexer_7 (
    .in0({bitfinder_2_found[21], B[20:0]}), .in1({bitfinder_1_found[21], A[20:0]}), .out(multiplexer_7_out),
    .sel(comparator_1_gt));
  Multiplexer #(.width(10)) multiplexer_8 (
    .in0(subtractor_1_out), .in1(10'h1f), .out(multiplexer_8_out), .sel(comparator_2_gt));
  BitFinder #(.width(31)) bitfinder_2 (.in(B[30:0]), .found(bitfinder_2_found[21]));  // open: index
  Multiplexer #(.width(22)) multiplexer_9 (
    .in0({bitfinder_1_found[21], A[20:0]}), .in1({bitfinder_2_found[21], B[20:0]}), .out(multiplexer_9_out),
    .sel(comparator_1_gt));
  Bit_Extender #(.in_width(10), .out_width(5), .\type ("zero")) bit_extender_1 (
    .in(multiplexer_8_out), .out(bit_extender_1_out));
  // Probe on bit_extender_1_out
  Negator #(.width(32)) negator_3 (.in({result_sign, adder_1_out}), .out(negator_3_out));
  // Probe on {bitfinder_2_found[21], B[20:0]}
  assign bit_extender_2_out = {{10{1'b0}}, multiplexer_9_out};  // Bit_Extender bit_extender_2
  Adder #(.width(32)) adder_1 (
    .a(multiplexer_3_out), .b(multiplexer_4_out), .out({result_sign, adder_1_out}));  // open: cin, cout
  Multiplexer #(.width(32)) multiplexer_10 (
    .in0({result_sign, adder_1_out}), .in1(negator_3_out), .out(multiplexer_10_out), .sel(result_sign));
  // Probe on multiplexer_10_out
  Shifter #(.width(32)) shifter_1 (.in(bit_extender_2_out), .\dist (5'b01000), .out(shifter_1_out));
  // Probe on {result_sign, adder_1_out}
  Bit_Extender #(.in_width(32), .out_width(31), .\type ("zero")) bit_extender_3 (
    .in(multiplexer_10_out), .out(bit_extender_3_out));
  // Probe on multiplexer_7_out
  Shifter #(.shift("lr"), .width(32)) shifter_2 (.in(shifter_1_out), .\dist (bit_extender_1_out), .out(shifter_2_out));
  // Probe on bit_extender_3_out
  assign bit_extender_4_out = {{10{1'b0}}, multiplexer_7_out};  // Bit_Extender bit_extender_4
  // Probe on shifter_2_out
  assign bit_extender_5_out = {{1{1'b0}}, multiplexer_5_out};  // Bit_Extender bit_extender_5
  // Probe on normalizer_2_1_result[30:8]
  // Probe on shifter_3_out
  Shifter #(.width(32)) shifter_3 (.in(bit_extender_4_out), .\dist (5'b01000), .out(shifter_3_out));
  normalizer_2 normalizer_2_1 (
    .significand(bit_extender_3_out), .normalizing_point(6'b011101), .result(normalizer_2_1_result),
    .difference(normalizer_2_1_difference));
  Comparator #(.mode("unsigned"), .width(31)) comparator_3 (
    .a({31{1'b0}}), .b(normalizer_2_1_result), .eq(comparator_3_eq));  // open: gt, lt
  _7404 u_7404_1 (
    .pin13(comparator_3_eq), .pin12(n7404_1_pin12));  // open: pin1, pin2, pin3, pin4, pin5, pin6, pin11, pin10, pin9, pin8
  BitFinder #(.\type ("high1"), .width(6)) bitfinder_3 (
    .in(normalizer_2_1_result[5:0]), .found(bitfinder_3_found));  // open: index
  Bit_Extender #(.in_width(23), .out_width(1)) bit_extender_6 (
    .in(normalizer_2_1_result[30:8]), .out(bit_extender_6_out));
  final_adder_2 final_adder_2_1 (
    .current_exp(bit_extender_5_out), .difference(normalizer_2_1_difference),
    .overflow(final_adder_2_1_overflow), .underflow(final_adder_2_1_underflow),
    .exponent(final_adder_2_1_exponent));
  Multiplexer #(.width(11)) multiplexer_11 (
    .in0(final_adder_2_1_exponent), .in1({11{1'b0}}), .out(multiplexer_11_out), .sel(comparator_3_eq));
  _7432 u_7432_1 (
    .pin4(final_adder_2_1_underflow), .pin5(n7432_1_pin5), .pin6(n7432_1_pin6),
    .pin10(final_adder_2_1_overflow), .pin9(n7432_1_pin9), .pin8(overflow));  // open: pin1, pin2, pin3, pin13, pin12, pin11
  assign bit_extender_7_out = {{22{1'b0}}, rounding_2_1_out_5};  // Bit_Extender bit_extender_7
  rounding_2 rounding_2_1 (
    .G(normalizer_2_1_result[7]), .R(normalizer_2_1_result[6]), .S(bitfinder_3_found),
    .lsb(bit_extender_6_out), .out_5(rounding_2_1_out_5));
  _7408 u_7408_1 (
    .pin4(n7432_1_pin6), .pin5(n7404_1_pin12), .pin6(underflow));  // open: pin1, pin2, pin3, pin13, pin12, pin11, pin10, pin9, pin8
  final_adder_2 final_adder_2_2 (
    .current_exp(multiplexer_11_out), .difference(normalizer_after_rounding_2_1_difference),
    .overflow(n7432_1_pin9), .underflow(n7432_1_pin5), .exponent(final_adder_2_2_exponent));
  normalizer_after_rounding_2 normalizer_after_rounding_2_1 (
    .in_1(adder_2_out), .result(normalizer_after_rounding_2_1_result),
    .difference(normalizer_after_rounding_2_1_difference));
  Adder #(.width(23)) adder_2 (
    .a(bit_extender_7_out), .b(normalizer_2_1_result[30:8]), .out(adder_2_out));  // open: cin, cout
  Bit_Extender #(.in_width(11), .out_width(10)) bit_extender_8 (.in(final_adder_2_2_exponent), .out(result_exp));
  Bit_Extender #(.in_width(23), .out_width(21), .\type ("zero")) bit_extender_9 (
    .in(normalizer_after_rounding_2_1_result), .out(result_frac));

  // Notes on the sheet:
  //   L sign
  //   -L
  //   -S
  //   signed L
  //   A exp
  //   S sign
  //   signed S
  //   A frac
  //   L(exp)
  //   S(exp)
  //   B exp
  //   L-S
  //   B frac
  //   A > B => A(larger)
  //   A <= B => A(smaller)
  //   S frac
  //   L frac
endmodule

module rounding_2 (
  input  G,
  input  R,
  input  S,
  input  lsb,
  output out_5
);

  wire n7432_1_pin11, n7432_1_pin12;

  _7432 u_7432_1 (
    .pin13(S), .pin12(n7432_1_pin12), .pin11(n7432_1_pin11), .pin10(R), .pin9(lsb), .pin8(n7432_1_pin12));  // open: pin1, pin2, pin3, pin4, pin5, pin6
  _7408 u_7408_1 (
    .pin1(n7432_1_pin11), .pin2(G), .pin3(out_5));  // open: pin4, pin5, pin6, pin13, pin12, pin11, pin10, pin9, pin8
endmodule

module normalizer_2 (
  input  [30:0] significand,
  input  [5:0] normalizing_point,
  output [30:0] result,
  output [5:0] difference
);

  wire bitfinder_1_found;
  wire [4:0] bitfinder_1_index, multiplexer_1_out, negator_1_out;
  wire [5:0] bit_extender_1_out, subtractor_1_out;
  wire [30:0] shifter_1_out, shifter_2_out;

  BitFinder #(.\type ("high1"), .width(31)) bitfinder_1 (
    .in(significand), .index(bitfinder_1_index), .found(bitfinder_1_found));
  assign bit_extender_1_out = {{1{1'b0}}, bitfinder_1_index};  // Bit_Extender bit_extender_1
  // Probe on normalizing_point
  // Probe on bit_extender_1_out
  // Probe on subtractor_1_out
  Subtractor #(.width(6)) subtractor_1 (
    .a(normalizing_point), .b(bit_extender_1_out), .out(subtractor_1_out));  // open: bin, bout
  Negator #(.width(5)) negator_1 (.in(subtractor_1_out[4:0]), .out(negator_1_out));
  Multiplexer #(.width(5)) multiplexer_1 (
    .in0(subtractor_1_out[4:0]), .in1(negator_1_out), .out(multiplexer_1_out), .sel(subtractor_1_out[5]));
  // Probe on multiplexer_1_out
  Multiplexer #(.width(6)) multiplexer_2 (
    .in0({6{1'b0}}), .in1(subtractor_1_out), .out(difference), .sel(bitfinder_1_found));
  Shifter #(.width(31)) shifter_1 (.in(significand), .\dist (multiplexer_1_out), .out(shifter_1_out));
  Shifter #(.shift("lr"), .width(31)) shifter_2 (.in(significand), .\dist (multiplexer_1_out), .out(shifter_2_out));
  Multiplexer #(.width(31)) multiplexer_3 (
    .in0(shifter_1_out), .in1(shifter_2_out), .out(result), .sel(subtractor_1_out[5]));
endmodule

module normalizer_after_rounding_2 (
  input  [22:0] in_1,
  output [22:0] result,
  output [5:0] difference
);

  wire [30:0] bit_extender_1_out, normalizer_2_1_result;

  assign bit_extender_1_out = {{8{1'b0}}, in_1};  // Bit_Extender bit_extender_1
  normalizer_2 normalizer_2_1 (
    .significand(bit_extender_1_out), .normalizing_point(6'b010101), .result(normalizer_2_1_result),
    .difference(difference));
  Bit_Extender #(.in_width(31), .out_width(23), .\type ("zero")) bit_extender_2 (
    .in(normalizer_2_1_result), .out(result));
endmodule

module final_adder_2 (
  input  [10:0] current_exp,
  input  [5:0] difference,
  output overflow,
  output underflow,
  output [10:0] exponent
);

  wire n7404_1_pin2, n7404_1_pin4, n7404_1_pin6, n7404_1_pin8, n7404_1_pin9, n7408_1_pin6, n7408_1_pin8,
       n7408_1_pin11;
  wire [5:0] negator_1_out;
  wire [9:0] bit_extender_1_out;
  wire [10:10] bit_extender_1_out_2;

  Negator #(.width(6)) negator_1 (.in(difference), .out(negator_1_out));
  assign {bit_extender_1_out_2[10], bit_extender_1_out} = {{5{negator_1_out[5]}}, negator_1_out};  // Bit_Extender bit_extender_1
  _7404 u_7404_1 (
    .pin1(current_exp[10]), .pin2(n7404_1_pin2), .pin3(bit_extender_1_out_2[10]), .pin4(n7404_1_pin4),
    .pin5(exponent[10]), .pin6(n7404_1_pin6), .pin9(n7404_1_pin9), .pin8(n7404_1_pin8));  // open: pin13, pin12, pin11, pin10
  BitFinder #(.\type ("low0"), .width(10)) bitfinder_1 (.in(exponent[9:0]), .found(n7404_1_pin9));  // open: index
  Adder #(.width(11)) adder_1 (
    .a(current_exp), .b({bit_extender_1_out_2[10], bit_extender_1_out}), .out(exponent));  // open: cin, cout
  _7408 u_7408_1 (
    .pin4(n7404_1_pin8), .pin5(n7404_1_pin6), .pin6(n7408_1_pin6), .pin13(n7404_1_pin4),
    .pin12(n7404_1_pin2), .pin11(n7408_1_pin11), .pin10(n7408_1_pin11), .pin9(exponent[10]),
    .pin8(n7408_1_pin8));  // open: pin1, pin2, pin3
  _7432 u_7432_1 (
    .pin10(n7408_1_pin6), .pin9(n7408_1_pin8), .pin8(overflow));  // open: pin1, pin2, pin3, pin4, pin5, pin6, pin13, pin12, pin11
  Comparator #(.width(11)) comparator_1 (.a(exponent), .b(11'h1), .lt(underflow));  // open: gt, eq
endmodule
