// Logisim project Adder_32bit.circ as structural Verilog: 4 circuits, main circuit Adder_32bit
module Adder_32bit (
  input  Cin,
  input  [31:0] A,
  input  [31:0] B,
  output [31:0] S,
  output Cout
);

  wire adder_16bit_1_cout;

  Adder_16bit adder_16bit_1 (.Cin(Cin), .A(A[15:0]), .B(B[15:0]), .S(S[15:0]), .Cout(adder_16bit_1_cout));
  Adder_16bit adder_16bit_2 (.Cin(adder_16bit_1_cout), .A(A[31:16]), .B(B[31:16]), .S(S[31:16]), .Cout(Cout));
endmodule

module Adder_16bit (
  input  Cin,
  input  [15:0] A,
  input  [15:0] B,
  output [15:0] S,
  output Cout
);

  wire adder_8bit_1_cout;

  Adder_8bit adder_8bit_1 (.Cin(Cin), .A(A[7:0]), .B(B[7:0]), .S(S[7:0]), .Cout(adder_8bit_1_cout));
  Adder_8bit adder_8bit_2 (.Cin(adder_8bit_1_cout), .A(A[15:8]), .B(B[15:8]), .S(S[15:8]), .Cout(Cout));
endmodule

module Adder_8bit (
  input  Cin,
  input  [7:0] A,
  input  [7:0] B,
  output [7:0] S,
  output Cout
);

  wire adder_4bit_1_cout;

  Adder_4bit adder_4bit_1 (.Cin(Cin), .A(A[3:0]), .B(B[3:0]), .S(S[3:0]), .Cout(adder_4bit_1_cout));
  Adder_4bit adder_4bit_2 (.Cin(adder_4bit_1_cout), .A(A[7:4]), .B(B[7:4]), .S(S[7:4]), .Cout(Cout));
endmodule

module Adder_4bit (
  input  Cin,
  input  [3:0] A,
  input  [3:0] B,
  output [3:0] S,
  output Cout
);

  _74283 u_74283_1 (
    .pin1(S[1]), .pin2(B[1]), .pin3(A[1]), .pin4(S[0]), .pin5(A[0]), .pin6(B[0]), .pin7(Cin), .pin15(B[2]),
    .pin14(A[2]), .pin13(S[2]), .pin12(A[3]), .pin11(B[3]), .pin10(S[3]), .pin9(Cout));

  // Notes on the sheet:
  //   4 bit Adder
endmodule
