// Logisim project B1_Group1.circ as structural Verilog: 14 circuits, main circuit Part2
module Part2 (
  input  [11:0] Exp,
  input  [31:0] L,
  input  L_Sign,
  input  [31:0] S,
  input  S_Sign,
  output Sign,
  output [11:0] Exponent,
  output [18:0] Fraction,
  output Overflow,
  output Underflow
);

  wire bitfinder_1_found, n7408_1_pin9, rounding_1_difference, undriven;
  wire [5:0] normalizer_1_difference;
  wire [11:0] exponentchanger_1_exp_out;
  wire [31:0] normalizer_1_normalized, rounding_1_r_output, significandadder_1_sum;

  SignificandAdder significandadder_1 (
    .A(L), .A_Sign(L_Sign), .B(S), .B_Sign(S_Sign), .Sum(significandadder_1_sum), .Sign(Sign));
  Normalizer normalizer_1 (
    .Denormalized(significandadder_1_sum), .Normalized(normalizer_1_normalized),
    .Difference(normalizer_1_difference));
  BitFinder #(.width(32)) bitfinder_1 (.in(significandadder_1_sum), .found(bitfinder_1_found));  // open: index
  // Probe on undriven
  Rounding rounding_1 (
    .R_Input(normalizer_1_normalized),
    .R_Output({rounding_1_r_output[31:29], Fraction, rounding_1_r_output[9:0]}),
    .Difference(rounding_1_difference));
  _7408 u_7408_1 (
    .pin10(bitfinder_1_found), .pin9(n7408_1_pin9), .pin8(Underflow));  // open: pin1, pin2, pin3, pin4, pin5, pin6, pin13, pin12, pin11
  ExponentChanger exponentchanger_1 (
    .Exp_In(Exp), .Diff1(normalizer_1_difference), .Diff2(rounding_1_difference),
    .Exp_Out(exponentchanger_1_exp_out), .Underflow(n7408_1_pin9), .Overflow(Overflow));
  Multiplexer #(.width(12)) multiplexer_1 (
    .in0({12{1'b0}}), .in1(exponentchanger_1_exp_out), .out(Exponent), .sel(bitfinder_1_found));

  // Notes on the sheet:
  //   Overflow/Underflow can happen
  //   Maximum, 1 right shift and 19 left shift
  //   from exp+1 to exp-19
  //   where 000<exp<FFF
  //   Only overflow can happen
  //   Maximum, 1 right shift
endmodule

module Negator_32bit (
  input  [31:0] A,
  input  S,
  output [31:0] Neg_A
);

  wire [31:0] negator_1_out;

  Negator #(.width(32)) negator_1 (.in(A), .out(negator_1_out));
  Multiplexer #(.width(32)) multiplexer_1 (.in0(A), .in1(negator_1_out), .out(Neg_A), .sel(S));
endmodule

module SignificandAdder (
  input  [31:0] A,
  input  A_Sign,
  input  [31:0] B,
  input  B_Sign,
  output [31:0] Sum,
  output Sign
);

  wire [30:0] adder_1_out;
  wire [31:0] negator_32bit_1_neg_a, negator_32bit_2_neg_a;

  Negator_32bit negator_32bit_1 (.A(A), .S(A_Sign), .Neg_A(negator_32bit_1_neg_a));
  Negator_32bit negator_32bit_2 (.A(B), .S(B_Sign), .Neg_A(negator_32bit_2_neg_a));
  Adder #(.width(32)) adder_1 (
    .a(negator_32bit_1_neg_a), .b(negator_32bit_2_neg_a), .out({Sign, adder_1_out}));  // open: cin, cout
  Negator_32bit negator_32bit_3 (.A({Sign, adder_1_out}), .S(Sign), .Neg_A(Sum));

  // Notes on the sheet:
  //   Negate significands based on sign bit
  //   Add significands
  //   Negate adder output based on sign bit
endmodule

module Normalizer (
  input  [31:0] Denormalized,
  output [31:0] Normalized,
  output [5:0] Difference
);

  wire bitfinder_1_found;
  wire [4:0] bitfinder_1_index, negator_5bit_1_neg_a;
  wire [5:0] bit_extender_1_out, subtractor_1_out;

  BitFinder #(.\type ("high1"), .width(32)) bitfinder_1 (
    .in(Denormalized), .index(bitfinder_1_index), .found(bitfinder_1_found));
  assign bit_extender_1_out = {{1{1'b0}}, bitfinder_1_index};  // Bit_Extender bit_extender_1
  Subtractor #(.width(6)) subtractor_1 (
    .a(bit_extender_1_out), .b(6'b011101), .out(subtractor_1_out));  // open: bin, bout
  Multiplexer #(.width(6)) multiplexer_1 (
    .in0({6{1'b0}}), .in1(subtractor_1_out), .out(Difference), .sel(bitfinder_1_found));
  Negator_5bit negator_5bit_1 (.A(subtractor_1_out[4:0]), .S(subtractor_1_out[5]), .Neg_A(negator_5bit_1_neg_a));
  UniversalShifter_32bit universalshifter_32bit_1 (
    .S_Input(Denormalized), .Distance(negator_5bit_1_neg_a), .S(subtractor_1_out[5]), .S_Output(Normalized));
endmodule

module Negator_5bit (
  input  [4:0] A,
  input  S,
  output [4:0] Neg_A
);

  wire [4:0] negator_1_out;

  Negator #(.width(5)) negator_1 (.in(A), .out(negator_1_out));
  Multiplexer #(.width(5)) multiplexer_1 (.in0(A), .in1(negator_1_out), .out(Neg_A), .sel(S));
endmodule

module UniversalShifter_32bit (
  input  [31:0] S_Input,
  input  [4:0] Distance,
  input  S,
  output [31:0] S_Output
);

  wire [31:0] shifter_1_out, shifter_2_out;

  Shifter #(.shift("lr"), .width(32)) shifter_1 (.in(S_Input), .\dist (Distance), .out(shifter_1_out));
  Shifter #(.width(32)) shifter_2 (.in(S_Input), .\dist (Distance), .out(shifter_2_out));
  Multiplexer #(.width(32)) multiplexer_1 (.in0(shifter_1_out), .in1(shifter_2_out), .out(S_Output), .sel(S));

  // Notes on the sheet:
  //   S = 0 -> Right Shift
  //   S = 1 -> Left Shift
endmodule

module Rounding (
  input  [31:0] R_Input,
  output [31:0] R_Output,
  output Difference
);

  wire bit_extender_1_out, bitfinder_1_found, n7408_1_pin3, n7432_1_pin8, n7432_1_pin11;
  wire [4:0] bit_extender_2_out;
  wire [21:0] adder_1_out;

  BitFinder #(.\type ("high1")) bitfinder_1 (.in(R_Input[7:0]), .found(bitfinder_1_found));  // open: index
  Bit_Extender #(.in_width(22), .out_width(1), .\type ("zero")) bit_extender_1 (
    .in(R_Input[31:10]), .out(bit_extender_1_out));
  _7432 u_7432_1 (
    .pin13(bitfinder_1_found), .pin12(R_Input[8]), .pin11(n7432_1_pin11), .pin10(n7432_1_pin11),
    .pin9(bit_extender_1_out), .pin8(n7432_1_pin8));  // open: pin1, pin2, pin3, pin4, pin5, pin6
  _7408 u_7408_1 (
    .pin1(n7432_1_pin8), .pin2(R_Input[9]), .pin3(n7408_1_pin3));  // open: pin4, pin5, pin6, pin13, pin12, pin11, pin10, pin9, pin8
  Adder #(.width(22)) adder_1 (
    .a({22{1'b0}}), .b(R_Input[31:10]), .out({adder_1_out[21], Difference, adder_1_out[19:0]}),
    .cin(n7408_1_pin3));  // open: cout
  assign bit_extender_2_out = {{4{1'b0}}, Difference};  // Bit_Extender bit_extender_2
  Shifter #(.shift("lr"), .width(32)) shifter_1 (
    .in({adder_1_out[21], Difference, adder_1_out[19:0], {10{1'b0}}}), .\dist (bit_extender_2_out),
    .out(R_Output));

  // Notes on the sheet:
  //   G.(LSB+R+S)
endmodule

module ExponentChanger (
  input  [11:0] Exp_In,
  input  [5:0] Diff1,
  input  Diff2,
  output [11:0] Exp_Out,
  output Underflow,
  output Overflow
);

  wire bitfinder_1_found, bitfinder_2_found;
  wire [12:0] adder_1_out, adder_2_out, bit_extender_1_out, bit_extender_2_out;

  assign bit_extender_1_out = {{1{1'b0}}, Exp_In};  // Bit_Extender bit_extender_1
  assign bit_extender_2_out = {{7{1'b0}}, Diff1};  // Bit_Extender bit_extender_2
  Adder #(.width(13)) adder_1 (.a(bit_extender_1_out), .b(bit_extender_2_out), .out(adder_1_out));  // open: cin, cout
  // Probe on adder_1_out
  Comparator #(.width(13)) comparator_1 (.a(adder_1_out), .b(13'h1), .lt(Underflow));  // open: gt, eq
  BitFinder #(.\type ("low0"), .width(13)) bitfinder_1 (.in(adder_1_out), .found(bitfinder_1_found));  // open: index
  Adder #(.width(13)) adder_2 (.a({13{1'b0}}), .b(adder_1_out), .out(adder_2_out), .cin(Diff2));  // open: cout
  Bit_Extender #(.in_width(13), .out_width(12), .\type ("zero")) bit_extender_3 (.in(adder_2_out), .out(Exp_Out));
  BitFinder #(.\type ("low0"), .width(13)) bitfinder_2 (.in(adder_2_out), .found(bitfinder_2_found));  // open: index
  _7400 u_7400_1 (
    .pin1(bitfinder_1_found), .pin2(bitfinder_2_found), .pin3(Overflow));  // open: pin4, pin5, pin6, pin13, pin12, pin11, pin10, pin9, pin8
endmodule

module FPA (
  input  A_Sign,
  input  B_Sign,
  input  [11:0] B_Exponent,
  input  [18:0] B_Fraction,
  input  [11:0] A_Exponent,
  input  [18:0] A_Fraction,
  output Underflow,
  output Overflow,
  output S_Sign,
  output [11:0] S_Exponent,
  output [18:0] S_Fraction
);

  wire part1_1_l_sign, part1_1_s_sign;
  wire [11:0] part1_1_l_exp;
  wire [31:0] part1_1_l_frac, part1_1_s_frac;

  Part1 part1_1 (
    .A_Fraction(A_Fraction), .A_Exponent(A_Exponent), .A_Sign(A_Sign), .B_Fraction(B_Fraction),
    .B_Exponent(B_Exponent), .B_Sign(B_Sign), .L_exp(part1_1_l_exp), .L_frac(part1_1_l_frac),
    .L_sign(part1_1_l_sign), .S_frac(part1_1_s_frac), .S_sign(part1_1_s_sign));
  Part2 part2_1 (
    .Exp(part1_1_l_exp), .L(part1_1_l_frac), .L_Sign(part1_1_l_sign), .S(part1_1_s_frac),
    .S_Sign(part1_1_s_sign), .Sign(S_Sign), .Exponent(S_Exponent), .Fraction(S_Fraction),
    .Overflow(Overflow), .Underflow(Underflow));

  // Notes on the sheet:
  //   Difference between two exponent should be < 30. Or else smaller number will become zero.
endmodule

module FP_Representer (
  input  [31:0] float,
  output [31:0] Fraction,
  output [11:0] Exponent,
  output Sign
);

  wire [19:19] bitfinder_1_found;

  BitFinder #(.width(31)) bitfinder_1 (.in(float[30:0]), .found(bitfinder_1_found[19]));  // open: index
  assign Fraction = {{12{1'b0}}, {bitfinder_1_found[19], float[18:0]}};  // Bit_Extender bit_extender_1

  assign Exponent = float[30:19];
  assign Sign = float[31];
endmodule

module Large_Small_Select (
  input  [31:0] Frac_A,
  input  [31:0] Frac_B,
  input  [11:0] Exp_A,
  input  [11:0] Exp_B,
  input  Sign_A,
  input  Sign_B,
  output L_sign,
  output S_sign,
  output [31:0] A_larger,
  output [31:0] A_smaller,
  output [11:0] L_exp,
  output [11:0] S_exp
);

  wire comparator_1_gt;

  Comparator #(.mode("unsigned"), .width(12)) comparator_1 (
    .a(Exp_A), .b(Exp_B), .gt(comparator_1_gt));  // open: eq, lt
  Multiplexer multiplexer_1 (.in0(Sign_B), .in1(Sign_A), .out(L_sign), .sel(comparator_1_gt));
  Multiplexer multiplexer_2 (.in0(Sign_A), .in1(Sign_B), .out(S_sign), .sel(comparator_1_gt));
  Multiplexer #(.width(32)) multiplexer_3 (.in0(Frac_B), .in1(Frac_A), .out(A_larger), .sel(comparator_1_gt));
  Multiplexer #(.width(32)) multiplexer_4 (.in0(Frac_A), .in1(Frac_B), .out(A_smaller), .sel(comparator_1_gt));
  Multiplexer #(.width(12)) multiplexer_5 (.in0(Exp_B), .in1(Exp_A), .out(L_exp), .sel(comparator_1_gt));
  Multiplexer #(.width(12)) multiplexer_6 (.in0(Exp_A), .in1(Exp_B), .out(S_exp), .sel(comparator_1_gt));
endmodule

module Exp_Comparator (
  input  [31:0] A_larger,
  input  [31:0] A_smaller,
  input  [11:0] L_exp,
  input  [11:0] S_exp,
  output [31:0] L_frac,
  output [31:0] S_frac
);

  wire comparator_1_gt;
  wire [4:0] bit_extender_1_out;
  wire [11:0] multiplexer_1_out, subtractor_1_out;
  wire [31:0] shifter_1_out;

  Subtractor #(.width(12)) subtractor_1 (.a(L_exp), .b(S_exp), .out(subtractor_1_out));  // open: bin, bout
  Comparator #(.mode("unsigned"), .width(12)) comparator_1 (
    .a(subtractor_1_out), .b(12'h1f), .gt(comparator_1_gt));  // open: eq, lt
  Multiplexer #(.width(12)) multiplexer_1 (
    .in0(subtractor_1_out), .in1(12'h1f), .out(multiplexer_1_out), .sel(comparator_1_gt));
  Bit_Extender #(.in_width(12), .out_width(5), .\type ("zero")) bit_extender_1 (
    .in(multiplexer_1_out), .out(bit_extender_1_out));
  Shifter #(.width(32)) shifter_1 (.in(A_smaller), .\dist (5'b01010), .out(shifter_1_out));
  Shifter #(.width(32)) shifter_2 (.in(A_larger), .\dist (5'b01010), .out(L_frac));
  Shifter #(.shift("lr"), .width(32)) shifter_3 (.in(shifter_1_out), .\dist (bit_extender_1_out), .out(S_frac));
endmodule

module Part1 (
  input  [18:0] A_Fraction,
  input  [11:0] A_Exponent,
  input  A_Sign,
  input  [18:0] B_Fraction,
  input  [11:0] B_Exponent,
  input  B_Sign,
  output [11:0] L_exp,
  output [31:0] L_frac,
  output L_sign,
  output [31:0] S_frac,
  output S_sign
);

  wire fp_representer_1_sign, fp_representer_2_sign;
  wire [11:0] fp_representer_1_exponent, fp_representer_2_exponent, large_small_select_1_s_exp;
  wire [31:0] fp_representer_1_fraction, fp_representer_2_fraction, large_small_select_1_a_larger,
       large_small_select_1_a_smaller;

  // Probe on {A_Sign, A_Exponent, A_Fraction}
  // Probe on {B_Sign, B_Exponent, B_Fraction}
  FP_Representer fp_representer_1 (
    .float({A_Sign, A_Exponent, A_Fraction}), .Fraction(fp_representer_1_fraction),
    .Exponent(fp_representer_1_exponent), .Sign(fp_representer_1_sign));
  FP_Representer fp_representer_2 (
    .float({B_Sign, B_Exponent, B_Fraction}), .Fraction(fp_representer_2_fraction),
    .Exponent(fp_representer_2_exponent), .Sign(fp_representer_2_sign));
  Large_Small_Select large_small_select_1 (
    .Frac_A(fp_representer_1_fraction), .Frac_B(fp_representer_2_fraction),
    .Exp_A(fp_representer_1_exponent), .Exp_B(fp_representer_2_exponent), .Sign_A(fp_representer_1_sign),
    .Sign_B(fp_representer_2_sign), .L_sign(L_sign), .S_sign(S_sign),
    .A_larger(large_small_select_1_a_larger), .A_smaller(large_small_select_1_a_smaller), .L_exp(L_exp),
    .S_exp(large_small_select_1_s_exp));
  Exp_Comparator exp_comparator_1 (
    .A_larger(large_small_select_1_a_larger), .A_smaller(large_small_select_1_a_smaller), .L_exp(L_exp),
    .S_exp(large_small_select_1_s_exp), .L_frac(L_frac), .S_frac(S_frac));
endmodule

module main (
  input  A_Sign,
  input  B_Sign,
  input  [11:0] B_Exponent,
  input  [18:0] B_Fraction,
  input  [11:0] A_Exponent,
  input  [18:0] A_Fraction,
  output Underflow,
  output Overflow,
  output S_Sign,
  output [11:0] S_Exponent,
  output [18:0] S_Fraction
);

  FPA fpa_1 (
    .A_Sign(A_Sign), .B_Sign(B_Sign), .B_Exponent(B_Exponent), .B_Fraction(B_Fraction),
    .A_Exponent(A_Exponent), .A_Fraction(A_Fraction), .Underflow(Underflow), .Overflow(Overflow),
    .S_Sign(S_Sign), .S_Exponent(S_Exponent), .S_Fraction(S_Fraction));

  // Notes on the sheet:
  //   Difference between two exponent should be < 30. Or else smaller number will become zero.
endmodule
