// Logisim project B1_Group1_.circ as structural Verilog: 33 circuits, main circuit Dihan
module Dihan (
  input  [11:0] Exp,
  input  [31:0] L,
  input  L_Sign,
  input  [31:0] S,
  input  S_Sign,
  output Sign,
  output [11:0] Exponent,
  output [18:0] Fraction,
  output Overflow,
  output Underflow
);

  wire n7408_1_pin9, nonzero_check_32bit_1_out_2, rounding_1_difference;
  wire [5:0] normalizer_1_difference;
  wire [31:0] normalizer_1_normalized, rounding_1_r_output, significandadder_1_sum;

  SignificandAdder significandadder_1 (
    .A(L), .A_Sign(L_Sign), .B(S), .B_Sign(S_Sign), .Sum(significandadder_1_sum), .Sign(Sign));
  Normalizer normalizer_1 (
    .Denormalized(significandadder_1_sum), .Normalized(normalizer_1_normalized),
    .Difference(normalizer_1_difference));
  Rounding rounding_1 (
    .R_Input(normalizer_1_normalized),
    .R_Output({rounding_1_r_output[31:29], Fraction, rounding_1_r_output[9:0]}),
    .Difference(rounding_1_difference));
  NonZero_Check_32bit nonzero_check_32bit_1 (.A(significandadder_1_sum), .out_2(nonzero_check_32bit_1_out_2));
  _7408 u_7408_1 (
    .pin10(nonzero_check_32bit_1_out_2), .pin9(n7408_1_pin9), .pin8(Underflow));  // open: pin1, pin2, pin3, pin4, pin5, pin6, pin13, pin12, pin11
  ExponentChanger exponentchanger_1 (
    .Exp_In(Exp), .Diff1(normalizer_1_difference), .Diff2(rounding_1_difference), .Exp_Out(Exponent),
    .Underflow(n7408_1_pin9), .Overflow(Overflow));

  // Notes on the sheet:
  //   Overflow/Underflow can happen
  //   Maximum, 1 right shift and 19 left shift
  //   from exp+1 to exp-19
  //   where 000<exp<FFF
  //   Only overflow can happen
  //   Maximum, 1 right shift
endmodule

module Negator_32 (
  input  [31:0] A,
  input  S,
  output [31:0] Neg_A
);

  wire [31:0] negator_32bit_1_neg_a;

  Negator_32bit negator_32bit_1 (.A(A), .Neg_A(negator_32bit_1_neg_a));
  MUX_32bit mux_32bit_1 (.A_0(A), .B_1(negator_32bit_1_neg_a), .S(S), .Y(Neg_A));
endmodule

module SignificandAdder (
  input  [31:0] A,
  input  A_Sign,
  input  [31:0] B,
  input  B_Sign,
  output [31:0] Sum,
  output Sign
);

  wire [30:0] adder_32bit_1_s;
  wire [31:0] negator_32_1_neg_a, negator_32_2_neg_a;

  Negator_32 negator_32_1 (.A(A), .S(A_Sign), .Neg_A(negator_32_1_neg_a));
  Negator_32 negator_32_2 (.A(B), .S(B_Sign), .Neg_A(negator_32_2_neg_a));
  Adder_32bit adder_32bit_1 (
    .A(negator_32_1_neg_a), .B(negator_32_2_neg_a), .S({Sign, adder_32bit_1_s}));  // open: Cin, Cout
  Negator_32 negator_32_3 (.A({Sign, adder_32bit_1_s}), .S(Sign), .Neg_A(Sum));

  // Notes on the sheet:
  //   Negate significands based on sign bit
  //   Add significands
  //   Negate adder output based on sign bit
endmodule

module Normalizer (
  input  [31:0] Denormalized,
  output [31:0] Normalized,
  output [5:0] Difference
);

  wire bitfinder_1_found;
  wire [4:0] bitfinder_1_index, negator_5bit_1_neg_a;
  wire [5:0] bit_extender_1_out, subtractor_1_out;

  BitFinder #(.\type ("high1"), .width(32)) bitfinder_1 (
    .in(Denormalized), .index(bitfinder_1_index), .found(bitfinder_1_found));
  assign bit_extender_1_out = {{1{1'b0}}, bitfinder_1_index};  // Bit_Extender bit_extender_1
  Subtractor #(.width(6)) subtractor_1 (
    .a(bit_extender_1_out), .b(6'b011101), .out(subtractor_1_out));  // open: bin, bout
  Multiplexer #(.width(6)) multiplexer_1 (
    .in0({6{1'b0}}), .in1(subtractor_1_out), .out(Difference), .sel(bitfinder_1_found));
  Negator_5bit negator_5bit_1 (.A(subtractor_1_out[4:0]), .S(subtractor_1_out[5]), .Neg_A(negator_5bit_1_neg_a));
  UniversalShifter_32bit universalshifter_32bit_1 (
    .S_Input(Denormalized), .Distance(negator_5bit_1_neg_a), .S(subtractor_1_out[5]), .S_Output(Normalized));
endmodule

module Negator_5bit (
  input  [4:0] A,
  input  S,
  output [4:0] Neg_A
);

  wire [4:0] negator_1_out;

  Negator #(.width(5)) negator_1 (.in(A), .out(negator_1_out));
  Multiplexer #(.width(5)) multiplexer_1 (.in0(A), .in1(negator_1_out), .out(Neg_A), .sel(S));
endmodule

module UniversalShifter_32bit (
  input  [31:0] S_Input,
  input  [4:0] Distance,
  input  S,
  output [31:0] S_Output
);

  wire [31:0] shifter_1_out, shifter_2_out;

  Shifter #(.shift("lr"), .width(32)) shifter_1 (.in(S_Input), .\dist (Distance), .out(shifter_1_out));
  Shifter #(.width(32)) shifter_2 (.in(S_Input), .\dist (Distance), .out(shifter_2_out));
  MUX_32bit mux_32bit_1 (.A_0(shifter_1_out), .B_1(shifter_2_out), .S(S), .Y(S_Output));

  // Notes on the sheet:
  //   S = 0 -> Right Shift
  //   S = 1 -> Left Shift
endmodule

module Rounding (
  input  [31:0] R_Input,
  output [31:0] R_Output,
  output Difference
);

  wire bit_extender_1_out, bitfinder_1_found, n7408_1_pin3, n7432_1_pin8, n7432_1_pin11;
  wire [4:0] bit_extender_2_out;
  wire [21:0] adder_1_out;

  BitFinder #(.\type ("high1")) bitfinder_1 (.in(R_Input[7:0]), .found(bitfinder_1_found));  // open: index
  Bit_Extender #(.in_width(22), .out_width(1), .\type ("zero")) bit_extender_1 (
    .in(R_Input[31:10]), .out(bit_extender_1_out));
  _7432 u_7432_1 (
    .pin13(bitfinder_1_found), .pin12(R_Input[8]), .pin11(n7432_1_pin11), .pin10(n7432_1_pin11),
    .pin9(bit_extender_1_out), .pin8(n7432_1_pin8));  // open: pin1, pin2, pin3, pin4, pin5, pin6
  _7408 u_7408_1 (
    .pin1(n7432_1_pin8), .pin2(R_Input[9]), .pin3(n7408_1_pin3));  // open: pin4, pin5, pin6, pin13, pin12, pin11, pin10, pin9, pin8
  Adder #(.width(22)) adder_1 (
    .a({22{1'b0}}), .b(R_Input[31:10]), .out({adder_1_out[21], Difference, adder_1_out[19:0]}),
    .cin(n7408_1_pin3));  // open: cout
  assign bit_extender_2_out = {{4{1'b0}}, Difference};  // Bit_Extender bit_extender_2
  Shifter #(.shift("lr"), .width(32)) shifter_1 (
    .in({adder_1_out[21], Difference, adder_1_out[19:0], {10{1'b0}}}), .\dist (bit_extender_2_out),
    .out(R_Output));

  // Notes on the sheet:
  //   G.(LSB+R+S)
endmodule

module ExponentChanger (
  input  [11:0] Exp_In,
  input  [5:0] Diff1,
  input  Diff2,
  output [11:0] Exp_Out,
  output Underflow,
  output Overflow
);

  wire bitfinder_1_found, bitfinder_2_found;
  wire [12:0] adder_1_out, adder_2_out, bit_extender_1_out, bit_extender_2_out;

  assign bit_extender_1_out = {{1{1'b0}}, Exp_In};  // Bit_Extender bit_extender_1
  assign bit_extender_2_out = {{7{1'b0}}, Diff1};  // Bit_Extender bit_extender_2
  Adder #(.width(13)) adder_1 (.a(bit_extender_1_out), .b(bit_extender_2_out), .out(adder_1_out));  // open: cin, cout
  // Probe on adder_1_out
  Comparator #(.width(13)) comparator_1 (.a(adder_1_out), .b(13'h1), .lt(Underflow));  // open: gt, eq
  BitFinder #(.\type ("low0"), .width(13)) bitfinder_1 (.in(adder_1_out), .found(bitfinder_1_found));  // open: index
  Adder #(.width(13)) adder_2 (.a({13{1'b0}}), .b(adder_1_out), .out(adder_2_out), .cin(Diff2));  // open: cout
  Bit_Extender #(.in_width(13), .out_width(12), .\type ("zero")) bit_extender_3 (.in(adder_2_out), .out(Exp_Out));
  BitFinder #(.\type ("low0"), .width(13)) bitfinder_2 (.in(adder_2_out), .found(bitfinder_2_found));  // open: index
  _7400 u_7400_1 (
    .pin1(bitfinder_1_found), .pin2(bitfinder_2_found), .pin3(Overflow));  // open: pin4, pin5, pin6, pin13, pin12, pin11, pin10, pin9, pin8
endmodule

module main (
  input  A_Sign,
  input  B_Sign,
  input  [11:0] B_Exponent,
  input  [18:0] B_Fraction,
  input  [11:0] A_Exponent,
  input  [18:0] A_Fraction,
  output Underflow,
  output Overflow,
  output S_Sign,
  output [11:0] S_Exponent,
  output [18:0] S_Fraction
);

  wire souvik_1_l_sign, souvik_1_s_sign;
  wire [11:0] souvik_1_l_exp;
  wire [31:0] souvik_1_l_frac, souvik_1_s_frac;

  Souvik souvik_1 (
    .A_Fraction(A_Fraction), .A_Exponent(A_Exponent), .A_Sign(A_Sign), .B_Fraction(B_Fraction),
    .B_Exponent(B_Exponent), .B_Sign(B_Sign), .L_exp(souvik_1_l_exp), .L_frac(souvik_1_l_frac),
    .L_sign(souvik_1_l_sign), .S_frac(souvik_1_s_frac), .S_sign(souvik_1_s_sign));
  Dihan dihan_1 (
    .Exp(souvik_1_l_exp), .L(souvik_1_l_frac), .L_Sign(souvik_1_l_sign), .S(souvik_1_s_frac),
    .S_Sign(souvik_1_s_sign), .Sign(S_Sign), .Exponent(S_Exponent), .Fraction(S_Fraction),
    .Overflow(Overflow), .Underflow(Underflow));

  // Notes on the sheet:
  //   Difference between two exponent should be < 30. Or else smaller number will become zero.
endmodule

module Adder_32bit (
  input  Cin,
  input  [31:0] A,
  input  [31:0] B,
  output [31:0] S,
  output Cout
);

  wire adder_16bit_1_cout;

  Adder_16bit adder_16bit_1 (.Cin(Cin), .A(A[15:0]), .B(B[15:0]), .S(S[15:0]), .Cout(adder_16bit_1_cout));
  Adder_16bit adder_16bit_2 (.Cin(adder_16bit_1_cout), .A(A[31:16]), .B(B[31:16]), .S(S[31:16]), .Cout(Cout));
endmodule

module Adder_16bit (
  input  Cin,
  input  [15:0] A,
  input  [15:0] B,
  output [15:0] S,
  output Cout
);

  wire adder_8bit_1_cout;

  Adder_8bit adder_8bit_1 (.Cin(Cin), .A(A[7:0]), .B(B[7:0]), .S(S[7:0]), .Cout(adder_8bit_1_cout));
  Adder_8bit adder_8bit_2 (.Cin(adder_8bit_1_cout), .A(A[15:8]), .B(B[15:8]), .S(S[15:8]), .Cout(Cout));
endmodule

module Adder_8bit (
  input  Cin,
  input  [7:0] A,
  input  [7:0] B,
  output [7:0] S,
  output Cout
);

  wire adder_4bit_1_cout;

  Adder_4bit adder_4bit_1 (.Cin(Cin), .A(A[3:0]), .B(B[3:0]), .S(S[3:0]), .Cout(adder_4bit_1_cout));
  Adder_4bit adder_4bit_2 (.Cin(adder_4bit_1_cout), .A(A[7:4]), .B(B[7:4]), .S(S[7:4]), .Cout(Cout));
endmodule

module Adder_4bit (
  input  Cin,
  input  [3:0] A,
  input  [3:0] B,
  output [3:0] S,
  output Cout
);

  _74283 u_74283_1 (
    .pin1(S[1]), .pin2(B[1]), .pin3(A[1]), .pin4(S[0]), .pin5(A[0]), .pin6(B[0]), .pin7(Cin), .pin15(B[2]),
    .pin14(A[2]), .pin13(S[2]), .pin12(A[3]), .pin11(B[3]), .pin10(S[3]), .pin9(Cout));

  // Notes on the sheet:
  //   4 bit Adder
endmodule

module Complement_4bit (
  input  [3:0] A,
  output [3:0] A_Comp
);

  _7404 u_7404_1 (
    .pin1(A[2]), .pin2(A_Comp[2]), .pin3(A[3]), .pin4(A_Comp[3]), .pin13(A[0]), .pin12(A_Comp[0]),
    .pin11(A[1]), .pin10(A_Comp[1]));  // open: pin5, pin6, pin9, pin8
endmodule

module Complement_8bit (
  input  [7:0] A,
  output [7:0] A_Comp
);

  Complement_4bit complement_4bit_1 (.A(A[3:0]), .A_Comp(A_Comp[3:0]));
  Complement_4bit complement_4bit_2 (.A(A[7:4]), .A_Comp(A_Comp[7:4]));
endmodule

module Complement_16bit (
  input  [15:0] A,
  output [15:0] A_Comp
);

  Complement_8bit complement_8bit_1 (.A(A[7:0]), .A_Comp(A_Comp[7:0]));
  Complement_8bit complement_8bit_2 (.A(A[15:8]), .A_Comp(A_Comp[15:8]));
endmodule

module Complement_32bit (
  input  [31:0] A,
  output [31:0] A_Comp
);

  Complement_16bit complement_16bit_1 (.A(A[15:0]), .A_Comp(A_Comp[15:0]));
  Complement_16bit complement_16bit_2 (.A(A[31:16]), .A_Comp(A_Comp[31:16]));
endmodule

module Souvik (
  input  [18:0] A_Fraction,
  input  [11:0] A_Exponent,
  input  A_Sign,
  input  [18:0] B_Fraction,
  input  [11:0] B_Exponent,
  input  B_Sign,
  output [11:0] L_exp,
  output [31:0] L_frac,
  output L_sign,
  output [31:0] S_frac,
  output S_sign
);

  wire representator_1_sign, representator_2_sign;
  wire [11:0] representator_1_exponent, representator_2_exponent, selector_1_s_exp;
  wire [31:0] representator_1_fraction, representator_2_fraction, selector_1_a_larger, selector_1_a_smaller;

  Representator representator_1 (
    .float({A_Sign, A_Exponent, A_Fraction}), .Fraction(representator_1_fraction),
    .Exponent(representator_1_exponent), .Sign(representator_1_sign));
  Representator representator_2 (
    .float({B_Sign, B_Exponent, B_Fraction}), .Fraction(representator_2_fraction),
    .Exponent(representator_2_exponent), .Sign(representator_2_sign));
  Selector selector_1 (
    .Frac_A(representator_1_fraction), .Frac_B(representator_2_fraction), .Exp_A(representator_1_exponent),
    .Exp_B(representator_2_exponent), .Sign_A(representator_1_sign), .Sign_B(representator_2_sign),
    .L_sign(L_sign), .S_sign(S_sign), .A_larger(selector_1_a_larger), .A_smaller(selector_1_a_smaller),
    .L_exp(L_exp), .S_exp(selector_1_s_exp));
  ExpComp expcomp_1 (
    .A_larger(selector_1_a_larger), .A_smaller(selector_1_a_smaller), .L_exp(L_exp),
    .S_exp(selector_1_s_exp), .L_frac(L_frac), .S_frac(S_frac));
endmodule

module Representator (
  input  [31:0] float,
  output [31:0] Fraction,
  output [11:0] Exponent,
  output Sign
);

  wire [19:19] undriven;

  assign Fraction = {{12{1'b0}}, {undriven[19], float[18:0]}};  // Bit_Extender bit_extender_1

  assign Exponent = float[30:19];
  assign Sign = float[31];
endmodule

module Selector (
  input  [31:0] Frac_A,
  input  [31:0] Frac_B,
  input  [11:0] Exp_A,
  input  [11:0] Exp_B,
  input  Sign_A,
  input  Sign_B,
  output L_sign,
  output S_sign,
  output [31:0] A_larger,
  output [31:0] A_smaller,
  output [11:0] L_exp,
  output [11:0] S_exp
);

  wire comparator_1_gt;

  Comparator #(.mode("unsigned"), .width(12)) comparator_1 (
    .a(Exp_A), .b(Exp_B), .gt(comparator_1_gt));  // open: eq, lt
  Multiplexer multiplexer_1 (.in0(Sign_B), .in1(Sign_A), .out(L_sign), .sel(comparator_1_gt));
  Multiplexer multiplexer_2 (.in0(Sign_A), .in1(Sign_B), .out(S_sign), .sel(comparator_1_gt));
  Multiplexer #(.width(32)) multiplexer_3 (.in0(Frac_B), .in1(Frac_A), .out(A_larger), .sel(comparator_1_gt));
  Multiplexer #(.width(32)) multiplexer_4 (.in0(Frac_A), .in1(Frac_B), .out(A_smaller), .sel(comparator_1_gt));
  Multiplexer #(.width(12)) multiplexer_5 (.in0(Exp_B), .in1(Exp_A), .out(L_exp), .sel(comparator_1_gt));
  Multiplexer #(.width(12)) multiplexer_6 (.in0(Exp_A), .in1(Exp_B), .out(S_exp), .sel(comparator_1_gt));
endmodule

module ExpComp (
  input  [31:0] A_larger,
  input  [31:0] A_smaller,
  input  [11:0] L_exp,
  input  [11:0] S_exp,
  output [31:0] L_frac,
  output [31:0] S_frac
);

  wire comparator_1_gt;
  wire [4:0] bit_extender_1_out;
  wire [11:0] multiplexer_1_out, subtractor_1_out;
  wire [31:0] shifter_1_out;

  Subtractor #(.width(12)) subtractor_1 (.a(L_exp), .b(S_exp), .out(subtractor_1_out));  // open: bin, bout
  Comparator #(.mode("unsigned"), .width(12)) comparator_1 (
    .a(subtractor_1_out), .b(12'h1f), .gt(comparator_1_gt));  // open: eq, lt
  Multiplexer #(.width(12)) multiplexer_1 (
    .in0(subtractor_1_out), .in1(12'h1f), .out(multiplexer_1_out), .sel(comparator_1_gt));
  Bit_Extender #(.in_width(12), .out_width(5), .\type ("zero")) bit_extender_1 (
    .in(multiplexer_1_out), .out(bit_extender_1_out));
  Shifter #(.width(32)) shifter_1 (.in(A_smaller), .\dist (5'b01010), .out(shifter_1_out));
  Shifter #(.width(32)) shifter_2 (.in(A_larger), .\dist (5'b01010), .out(L_frac));
  Shifter #(.shift("lr"), .width(32)) shifter_3 (.in(shifter_1_out), .\dist (bit_extender_1_out), .out(S_frac));
endmodule

module Subtractor_32bit (
  input  [31:0] A,
  input  [31:0] B,
  output [31:0] S,
  output out_4
);

  wire n7404_1_pin9;
  wire [31:0] complement_32bit_1_a_comp;

  Complement_32bit complement_32bit_1 (.A(B), .A_Comp(complement_32bit_1_a_comp));
  _7404 u_7404_1 (
    .pin9(n7404_1_pin9), .pin8(out_4));  // open: pin1, pin2, pin3, pin4, pin5, pin6, pin13, pin12, pin11, pin10
  Adder_32bit adder_32bit_1 (.Cin(1'b1), .A(A), .B(complement_32bit_1_a_comp), .S(S), .Cout(n7404_1_pin9));
endmodule

module Negator_32bit (
  input  [31:0] A,
  output [31:0] Neg_A
);

  wire [31:0] complement_32bit_1_a_comp;

  Complement_32bit complement_32bit_1 (.A(A), .A_Comp(complement_32bit_1_a_comp));
  Adder_32bit adder_32bit_1 (.Cin(1'b1), .A(complement_32bit_1_a_comp), .B({32{1'b0}}), .S(Neg_A));  // open: Cout
endmodule

module MUX_4bit (
  input  [3:0] A,
  input  [3:0] B,
  input  S,
  output [3:0] Y
);

  wire n74157_1_pin15;

  _74157 u_74157_1 (
    .pin1(S), .pin2(A[0]), .pin3(B[0]), .pin4(Y[0]), .pin5(A[1]), .pin6(B[1]), .pin7(Y[1]),
    .pin15(n74157_1_pin15), .pin14(A[3]), .pin13(B[3]), .pin12(Y[3]), .pin11(A[2]), .pin10(B[2]), .pin9(Y[2]));
  // also tied to GND on the sheet: n74157_1_pin15
endmodule

module MUX_8bit (
  input  [7:0] A,
  input  [7:0] B,
  input  S,
  output [7:0] Y
);

  MUX_4bit mux_4bit_1 (.A(A[3:0]), .B(B[3:0]), .S(S), .Y(Y[3:0]));
  MUX_4bit mux_4bit_2 (.A(A[7:4]), .B(B[7:4]), .S(S), .Y(Y[7:4]));
endmodule

module MUX_16bit (
  input  [15:0] A,
  input  [15:0] B,
  input  S,
  output [15:0] Y
);

  MUX_8bit mux_8bit_1 (.A(A[7:0]), .B(B[7:0]), .S(S), .Y(Y[7:0]));
  MUX_8bit mux_8bit_2 (.A(A[15:8]), .B(B[15:8]), .S(S), .Y(Y[15:8]));
endmodule

module MUX_32bit (
  input  [31:0] A_0,
  input  [31:0] B_1,
  input  S,
  output [31:0] Y
);

  MUX_16bit mux_16bit_1 (.A(A_0[15:0]), .B(B_1[15:0]), .S(S), .Y(Y[15:0]));
  MUX_16bit mux_16bit_2 (.A(A_0[31:16]), .B(B_1[31:16]), .S(S), .Y(Y[31:16]));
endmodule

module OR_4bit (
  input  [3:0] A,
  input  [3:0] B,
  output [3:0] Y
);

  _7432 u_7432_1 (
    .pin1(A[0]), .pin2(B[0]), .pin3(Y[0]), .pin4(A[1]), .pin5(B[1]), .pin6(Y[1]), .pin13(A[2]), .pin12(B[2]),
    .pin11(Y[2]), .pin10(A[3]), .pin9(B[3]), .pin8(Y[3]));
endmodule

module OR_8bit (
  input  [7:0] A,
  input  [7:0] B,
  output [7:0] Y
);

  OR_4bit or_4bit_1 (.A(A[3:0]), .B(B[3:0]), .Y(Y[3:0]));
  OR_4bit or_4bit_2 (.A(A[7:4]), .B(B[7:4]), .Y(Y[7:4]));
endmodule

module OR_16bit (
  input  [15:0] A,
  input  [15:0] B,
  output [15:0] Y
);

  OR_8bit or_8bit_1 (.A(A[7:0]), .B(B[7:0]), .Y(Y[7:0]));
  OR_8bit or_8bit_2 (.A(A[15:8]), .B(B[15:8]), .Y(Y[15:8]));
endmodule

module OR_32bit (
  input  [31:0] A_0,
  input  [31:0] B_1,
  output [31:0] Y
);

  OR_16bit or_16bit_1 (.A(A_0[15:0]), .B(B_1[15:0]), .Y(Y[15:0]));
  OR_16bit or_16bit_2 (.A(A_0[31:16]), .B(B_1[31:16]), .Y(Y[31:16]));
endmodule

module Comparator_32bit (
  input  [31:0] A,
  input  [31:0] B,
  output Larger,
  output Equal,
  output Smaller
);

  wire n7408_1_pin5, nonzero_check_32bit_1_out_2;
  wire [31:0] subtractor_32bit_1_s;

  Subtractor_32bit subtractor_32bit_1 (.A(A), .B(B), .S(subtractor_32bit_1_s), .out_4(Smaller));
  NonZero_Check_32bit nonzero_check_32bit_1 (.A(subtractor_32bit_1_s), .out_2(nonzero_check_32bit_1_out_2));
  _7408 u_7408_1 (
    .pin4(nonzero_check_32bit_1_out_2), .pin5(n7408_1_pin5), .pin6(Larger));  // open: pin1, pin2, pin3, pin13, pin12, pin11, pin10, pin9, pin8
  _7436 u_7436_1 (
    .pin13(Smaller), .pin12(nonzero_check_32bit_1_out_2), .pin11(Equal));  // open: pin1, pin2, pin3, pin4, pin5, pin6, pin10, pin9, pin8
  _7404 u_7404_1 (
    .pin13(Smaller), .pin12(n7408_1_pin5));  // open: pin1, pin2, pin3, pin4, pin5, pin6, pin11, pin10, pin9, pin8
endmodule

module NonZero_Check_32bit (
  input  [31:0] A,
  output out_2
);

  wire n7432_1_pin2, n7432_1_pin3, n7432_1_pin5, n7432_1_pin11, n7432_2_pin2, n7432_2_pin3, n7432_2_pin5,
       n7432_2_pin11, n7432_3_pin2, n7432_3_pin3, n7432_3_pin5, n7432_3_pin11, n7432_4_pin2, n7432_4_pin3,
       n7432_4_pin5, n7432_4_pin11, n7432_5_pin2, n7432_5_pin3, n7432_5_pin5, n7432_5_pin11, n7432_6_pin2,
       n7432_6_pin3, n7432_6_pin5, n7432_6_pin11, n7432_7_pin2, n7432_7_pin3, n7432_7_pin5, n7432_7_pin11,
       n7432_8_pin5, n7432_8_pin11;

  _7432 u_7432_1 (
    .pin1(A[4]), .pin2(n7432_1_pin2), .pin3(n7432_1_pin3), .pin4(A[3]), .pin5(n7432_1_pin5),
    .pin6(n7432_1_pin2), .pin13(A[2]), .pin12(A[1]), .pin11(n7432_1_pin11), .pin10(n7432_1_pin11),
    .pin9(A[0]), .pin8(n7432_1_pin5));
  _7432 u_7432_2 (
    .pin1(A[8]), .pin2(n7432_2_pin2), .pin3(n7432_2_pin3), .pin4(A[7]), .pin5(n7432_2_pin5),
    .pin6(n7432_2_pin2), .pin13(A[5]), .pin12(n7432_1_pin3), .pin11(n7432_2_pin11), .pin10(n7432_2_pin11),
    .pin9(A[6]), .pin8(n7432_2_pin5));
  _7432 u_7432_3 (
    .pin1(A[12]), .pin2(n7432_3_pin2), .pin3(n7432_3_pin3), .pin4(A[11]), .pin5(n7432_3_pin5),
    .pin6(n7432_3_pin2), .pin13(A[9]), .pin12(n7432_2_pin3), .pin11(n7432_3_pin11), .pin10(n7432_3_pin11),
    .pin9(A[10]), .pin8(n7432_3_pin5));
  _7432 u_7432_4 (
    .pin1(A[16]), .pin2(n7432_4_pin2), .pin3(n7432_4_pin3), .pin4(A[15]), .pin5(n7432_4_pin5),
    .pin6(n7432_4_pin2), .pin13(A[13]), .pin12(n7432_3_pin3), .pin11(n7432_4_pin11), .pin10(n7432_4_pin11),
    .pin9(A[14]), .pin8(n7432_4_pin5));
  _7432 u_7432_5 (
    .pin1(A[20]), .pin2(n7432_5_pin2), .pin3(n7432_5_pin3), .pin4(A[19]), .pin5(n7432_5_pin5),
    .pin6(n7432_5_pin2), .pin13(A[17]), .pin12(n7432_4_pin3), .pin11(n7432_5_pin11), .pin10(n7432_5_pin11),
    .pin9(A[18]), .pin8(n7432_5_pin5));
  _7432 u_7432_6 (
    .pin1(A[24]), .pin2(n7432_6_pin2), .pin3(n7432_6_pin3), .pin4(A[23]), .pin5(n7432_6_pin5),
    .pin6(n7432_6_pin2), .pin13(A[21]), .pin12(n7432_5_pin3), .pin11(n7432_6_pin11), .pin10(n7432_6_pin11),
    .pin9(A[22]), .pin8(n7432_6_pin5));
  _7432 u_7432_7 (
    .pin1(A[28]), .pin2(n7432_7_pin2), .pin3(n7432_7_pin3), .pin4(A[27]), .pin5(n7432_7_pin5),
    .pin6(n7432_7_pin2), .pin13(A[25]), .pin12(n7432_6_pin3), .pin11(n7432_7_pin11), .pin10(n7432_7_pin11),
    .pin9(A[26]), .pin8(n7432_7_pin5));
  _7432 u_7432_8 (
    .pin4(A[31]), .pin5(n7432_8_pin5), .pin6(out_2), .pin13(A[29]), .pin12(n7432_7_pin3),
    .pin11(n7432_8_pin11), .pin10(n7432_8_pin11), .pin9(A[30]), .pin8(n7432_8_pin5));  // open: pin1, pin2, pin3
endmodule
