// Logisim project B1_Group1_Souvik.circ as structural Verilog: 4 circuits, main circuit Souvik
module Souvik (
  input  [18:0] A_Fraction,
  input  [11:0] A_Exponent,
  input  A_Sign,
  input  [18:0] B_Fraction,
  input  [11:0] B_Exponent,
  input  B_Sign,
  output [11:0] L_exp,
  output [31:0] L_frac,
  output L_sign,
  output [31:0] S_frac,
  output S_sign
);

  wire floating_point_representatior_1_sign, floating_point_representatior_2_sign;
  wire [11:0] floating_point_representatior_1_exponent, floating_point_representatior_2_exponent,
       selector_1_s_exp;
  wire [31:0] floating_point_representatior_1_fraction, floating_point_representatior_2_fraction,
       selector_1_a_larger, selector_1_a_smaller;

  Floating_point_representatior floating_point_representatior_1 (
    .float({A_Sign, A_Exponent, A_Fraction}), .Fraction(floating_point_representatior_1_fraction),
    .Exponent(floating_point_representatior_1_exponent), .Sign(floating_point_representatior_1_sign));
  Floating_point_representatior floating_point_representatior_2 (
    .float({B_Sign, B_Exponent, B_Fraction}), .Fraction(floating_point_representatior_2_fraction),
    .Exponent(floating_point_representatior_2_exponent), .Sign(floating_point_representatior_2_sign));
  Selector selector_1 (
    .Frac_A(floating_point_representatior_1_fraction), .Frac_B(floating_point_representatior_2_fraction),
    .Exp_A(floating_point_representatior_1_exponent), .Exp_B(floating_point_representatior_2_exponent),
    .Sign_A(floating_point_representatior_1_sign), .Sign_B(floating_point_representatior_2_sign),
    .L_sign(L_sign), .S_sign(S_sign), .A_larger(selector_1_a_larger), .A_smaller(selector_1_a_smaller),
    .L_exp(L_exp), .S_exp(selector_1_s_exp));
  ExpComparator expcomparator_1 (
    .A_larger(selector_1_a_larger), .A_smaller(selector_1_a_smaller), .L_exp(L_exp),
    .S_exp(selector_1_s_exp), .L_frac(L_frac), .S_frac(S_frac));
endmodule

module Floating_point_representatior (
  input  [31:0] float,
  output [31:0] Fraction,
  output [11:0] Exponent,
  output Sign
);

  wire [19:19] bitfinder_1_found;

  BitFinder #(.width(31)) bitfinder_1 (.in(float[30:0]), .found(bitfinder_1_found[19]));  // open: index
  assign Fraction = {{12{1'b0}}, {bitfinder_1_found[19], float[18:0]}};  // Bit_Extender bit_extender_1

  assign Exponent = float[30:19];
  assign Sign = float[31];
endmodule

module Selector (
  input  [31:0] Frac_A,
  input  [31:0] Frac_B,
  input  [11:0] Exp_A,
  input  [11:0] Exp_B,
  input  Sign_A,
  input  Sign_B,
  output L_sign,
  output S_sign,
  output [31:0] A_larger,
  output [31:0] A_smaller,
  output [11:0] L_exp,
  output [11:0] S_exp
);

  wire comparator_1_gt;

  Comparator #(.mode("unsigned"), .width(12)) comparator_1 (
    .a(Exp_A), .b(Exp_B), .gt(comparator_1_gt));  // open: eq, lt
  Multiplexer multiplexer_1 (.in0(Sign_B), .in1(Sign_A), .out(L_sign), .sel(comparator_1_gt));
  Multiplexer multiplexer_2 (.in0(Sign_A), .in1(Sign_B), .out(S_sign), .sel(comparator_1_gt));
  Multiplexer #(.width(32)) multiplexer_3 (.in0(Frac_B), .in1(Frac_A), .out(A_larger), .sel(comparator_1_gt));
  Multiplexer #(.width(32)) multiplexer_4 (.in0(Frac_A), .in1(Frac_B), .out(A_smaller), .sel(comparator_1_gt));
  Multiplexer #(.width(12)) multiplexer_5 (.in0(Exp_B), .in1(Exp_A), .out(L_exp), .sel(comparator_1_gt));
  Multiplexer #(.width(12)) multiplexer_6 (.in0(Exp_A), .in1(Exp_B), .out(S_exp), .sel(comparator_1_gt));
endmodule

module ExpComparator (
  input  [31:0] A_larger,
  input  [31:0] A_smaller,
  input  [11:0] L_exp,
  input  [11:0] S_exp,
  output [31:0] L_frac,
  output [31:0] S_frac
);

  wire comparator_1_gt;
  wire [4:0] bit_extender_1_out;
  wire [11:0] multiplexer_1_out, subtractor_1_out;
  wire [31:0] shifter_1_out;

  Subtractor #(.width(12)) subtractor_1 (.a(L_exp), .b(S_exp), .out(subtractor_1_out));  // open: bin, bout
  Comparator #(.mode("unsigned"), .width(12)) comparator_1 (
    .a(subtractor_1_out), .b(12'h1f), .gt(comparator_1_gt));  // open: eq, lt
  Multiplexer #(.width(12)) multiplexer_1 (
    .in0(subtractor_1_out), .in1(12'h1f), .out(multiplexer_1_out), .sel(comparator_1_gt));
  Bit_Extender #(.in_width(12), .out_width(5), .\type ("zero")) bit_extender_1 (
    .in(multiplexer_1_out), .out(bit_extender_1_out));
  Shifter #(.width(32)) shifter_1 (.in(A_smaller), .\dist (5'b01010), .out(shifter_1_out));
  Shifter #(.width(32)) shifter_2 (.in(A_larger), .\dist (5'b01010), .out(L_frac));
  Shifter #(.shift("lr"), .width(32)) shifter_3 (.in(shifter_1_out), .\dist (bit_extender_1_out), .out(S_frac));
endmodule
