// Logisim project 4bit-Mips.circ as structural Verilog
module main (
  input  in_1,
  output [3:0] t0,
  output [3:0] t1,
  output [3:0] t2,
  output [3:0] t3,
  output [3:0] t4
);

  wire alu_1_p4, clock_1_out, control_1_p2, control_1_p3, control_1_p4, control_1_p6, control_1_p7,
       control_1_p8, control_1_p9, control_1_p10, instruction_1_p5, instruction_1_p6, multiplexer_4_out,
       registers_1_p6, registers_1_p9, registers_1_p11;
  wire [3:0] alu_1_p5, data_memory_1_p7, instruction_1_p7, instruction_1_p8, multiplexer_1_out,
       multiplexer_2_out, registers_1_p4, registers_1_p10;
  wire [7:0] adder_1_out, adder_2_out, bit_extender_1_out, instruction_1_p1, instruction_1_p4,
       instruction_1_p9, multiplexer_3_out;

  // Probe on instruction_1_p1
  Clock clock_1 (.out(clock_1_out));
  // Probe on instruction_1_p4
  Adder adder_1 (.a(instruction_1_p4), .b(8'h1), .out(adder_1_out));  // open: cin, cout
  // Probe on instruction_1_p5
  // Instruction instruction_1: pin names not known; wires that end beside it: instruction_1_p1, clock_1_out, in_1, instruction_1_p4, instruction_1_p5, instruction_1_p6, instruction_1_p7, instruction_1_p8, instruction_1_p9
  // Probe on instruction_1_p6
  // Probe on instruction_1_p7
  // Probe on instruction_1_p8
  assign bit_extender_1_out = {{4{1'b0}}, instruction_1_p8};  // Bit_Extender bit_extender_1
  Multiplexer #(.width(4), .enable("false")) multiplexer_1 (
    .in0(instruction_1_p7), .in1(instruction_1_p8), .out(multiplexer_1_out), .sel(control_1_p2));
  // Probe on multiplexer_1_out
  // Registers registers_1: pin names not known; wires that end beside it: instruction_1_p6, instruction_1_p7, multiplexer_1_out, registers_1_p4, in_1, registers_1_p6, clock_1_out, {t4, t3, t2, t1, t0}, registers_1_p9, registers_1_p10, registers_1_p11
  Adder adder_2 (.a(bit_extender_1_out), .b(adder_1_out), .out(adder_2_out));  // open: cin, cout
  // Control control_1: pin names not known; wires that end beside it: instruction_1_p5, control_1_p2, control_1_p3, control_1_p4, registers_1_p6, control_1_p6, control_1_p7, control_1_p8, control_1_p9, control_1_p10
  // Probe on registers_1_p9
  Multiplexer #(.width(4), .enable("false")) multiplexer_2 (
    .in0(registers_1_p10), .in1(instruction_1_p8), .out(multiplexer_2_out), .sel(control_1_p3));
  Multiplexer #(.width(8), .enable("false")) multiplexer_3 (
    .in0(adder_1_out), .in1(adder_2_out), .out(multiplexer_3_out), .sel(multiplexer_4_out));
  Multiplexer #(.enable("false")) multiplexer_4 (
    .in0(control_1_p9), .in1(control_1_p8), .out(multiplexer_4_out), .sel(alu_1_p4));
  // Probe on multiplexer_2_out
  // MIPS_ALU alu_1: pin names not known; wires that end beside it: registers_1_p11, registers_1_p9, multiplexer_2_out, alu_1_p4, alu_1_p5
  // Probe on alu_1_p5
  // Probe on registers_1_p10
  Multiplexer #(.width(8), .enable("false")) multiplexer_5 (
    .in0(multiplexer_3_out), .in1(instruction_1_p9), .out(instruction_1_p1), .sel(control_1_p10));
  // Data_Memory data_memory_1: pin names not known; wires that end beside it: alu_1_p5, registers_1_p10, clock_1_out, control_1_p6, in_1, control_1_p7, data_memory_1_p7
  Multiplexer #(.width(4), .enable("false")) multiplexer_6 (
    .in0(alu_1_p5), .in1(data_memory_1_p7), .out(registers_1_p4), .sel(control_1_p4));
endmodule

module Instruction_Memory (
  input  [7:0] Red_Address,
  output [3:0] _12_15,
  output [3:0] _8_11,
  output [3:0] _4_7,
  output [3:0] _0_3,
  output [7:0] _0_7
);

  ROM #(.dataWidth(16)) rom_1 (.addr(Red_Address), .data({_12_15, _8_11, _0_7[3:0], _0_3}), .sel(1'b1));

  assign _0_7[7:4] = _0_3;
  assign _4_7 = _0_7[3:0];
endmodule

module Register_File (
  input  RegWrite,
  input  CLK,
  input  [3:0] Dst_Reg_1,
  input  [3:0] WriteData,
  input  CLR,
  input  [3:0] SrcReg1,
  input  [3:0] SrcReg2,
  output [19:0] t4__t3__t2__t1__t0,
  output [3:0] Read_Data_1,
  output [3:0] Read_Data_2
);

  wire and_1_out, demultiplexer_1_out1, demultiplexer_1_out2, demultiplexer_1_out3, demultiplexer_1_out4,
       demultiplexer_1_out6, demultiplexer_1_out7, not_1_out, not_2_out, not_3_out, not_4_out, not_5_out,
       not_6_out;
  wire [3:0] sp_q;

  not not_1 (not_1_out, demultiplexer_1_out1);
  not not_2 (not_2_out, demultiplexer_1_out2);
  Register #(.width(4)) t1 (.D(WriteData), .Q(t4__t3__t2__t1__t0[7:4]), .clk(not_1_out), .clr(CLR));  // open: en
  Multiplexer #(.select(3), .width(4), .enable("false")) multiplexer_1 (
    .in0(4'b0000), .in1(t4__t3__t2__t1__t0[7:4]), .in2(t4__t3__t2__t1__t0[11:8]),
    .in3(t4__t3__t2__t1__t0[15:12]), .in4(t4__t3__t2__t1__t0[19:16]), .in5(4'b0000), .in6(sp_q),
    .in7(t4__t3__t2__t1__t0[3:0]), .out(Read_Data_1), .sel(SrcReg1[2:0]));
  Demultiplexer #(.select(3), .enable("false")) demultiplexer_1 (
    .out1(demultiplexer_1_out1), .out2(demultiplexer_1_out2), .out3(demultiplexer_1_out3),
    .out4(demultiplexer_1_out4), .out6(demultiplexer_1_out6), .out7(demultiplexer_1_out7), .in(and_1_out),
    .sel(Dst_Reg_1[2:0]));  // open: out0, out5
  not not_3 (not_3_out, demultiplexer_1_out3);
  Register #(.width(4)) t2 (.D(WriteData), .Q(t4__t3__t2__t1__t0[11:8]), .clk(not_2_out), .clr(CLR));  // open: en
  and and_1 (and_1_out, RegWrite, CLK);
  not not_4 (not_4_out, demultiplexer_1_out4);
  Register #(.width(4)) t3 (.D(WriteData), .Q(t4__t3__t2__t1__t0[15:12]), .clk(not_3_out), .clr(CLR));  // open: en
  Multiplexer #(.select(3), .width(4), .enable("false")) multiplexer_2 (
    .in0(4'b0000), .in1(t4__t3__t2__t1__t0[7:4]), .in2(t4__t3__t2__t1__t0[11:8]),
    .in3(t4__t3__t2__t1__t0[15:12]), .in4(t4__t3__t2__t1__t0[19:16]), .in5(4'b0000), .in6(sp_q),
    .in7(t4__t3__t2__t1__t0[3:0]), .out(Read_Data_2), .sel(SrcReg2[2:0]));
  not not_5 (not_5_out, demultiplexer_1_out7);
  Register #(.width(4)) t4 (.D(WriteData), .Q(t4__t3__t2__t1__t0[19:16]), .clk(not_4_out), .clr(CLR));  // open: en
  not not_6 (not_6_out, demultiplexer_1_out6);
  Register #(.width(4)) t0 (.D(WriteData), .Q(t4__t3__t2__t1__t0[3:0]), .clk(not_5_out), .clr(CLR));  // open: en
  Register #(.width(4)) sp (.D(WriteData), .Q(sp_q), .clk(not_6_out), .clr(CLR));  // open: en

  // Notes on the sheet:
  //   $zero
endmodule

module ALU (
  input  [2:0] ALUOp,
  input  [3:0] A,
  input  [3:0] B,
  output [3:0] Output,
  output Zero_flag
);

  wire [3:0] adder_1_out, and_1_out, nor_1_out, or_1_out, shifter_1_out, shifter_2_out, subtractor_1_out;

  Adder #(.width(4)) adder_1 (.a(A), .b(B), .out(adder_1_out), .cin(1'b0));  // open: cout
  Subtractor #(.width(4)) subtractor_1 (.a(A), .b(B), .out(subtractor_1_out), .bin(1'b0));  // open: bout
  assign and_1_out = A & B;  // AND_Gate and_1, 4 bits wide
  assign or_1_out = A | B;  // OR_Gate or_1, 4 bits wide
  assign nor_1_out = ~(A | B);  // NOR_Gate nor_1, 4 bits wide
  Shifter #(.width(4)) shifter_1 (.in(A), .\dist (B[1:0]), .out(shifter_1_out));
  Shifter #(.width(4), .shift("lr")) shifter_2 (.in(A), .\dist (B[1:0]), .out(shifter_2_out));
  Multiplexer #(.select(3), .width(4), .enable("false")) multiplexer_1 (
    .in0(adder_1_out), .in1(subtractor_1_out), .in2(and_1_out), .in3(or_1_out), .in4(nor_1_out),
    .in5(shifter_1_out), .in6(shifter_2_out), .in7(4'b0000), .out(Output), .sel(ALUOp));
  nor nor_2 (Zero_flag, Output[0], Output[1], Output[2], Output[3]);
endmodule

// Instructionn Memory
module Control_Unit (
  input  [3:0] OP_Code,
  output [2:0] ALUOp,
  output Jump,
  output bneq,
  output beq,
  output MemWrite,
  output MemRead,
  output RegWrite,
  output MemToReg,
  output ALUSrc,
  output RegDst
);

  ROM #(.addrWidth(4), .dataWidth(12)) rom_1 (
    .addr(OP_Code), .data({RegDst, ALUSrc, MemToReg, RegWrite, MemRead, MemWrite, beq, bneq, Jump, ALUOp}));  // open: sel

  // Notes on the sheet:
  //   contents of rom_1 (hex, n*v repeats v):
  //   902 505 500 503 903 640 901 501 21 502 8 904 11 780 900 506
endmodule

module Memory (
  input  MemRead,
  input  MemWrite,
  input  [3:0] Address,
  input  [3:0] Write_Data,
  input  CLK,
  input  CLR,
  output [3:0] Data_Read
);

  wire not_1_out;

  not not_1 (not_1_out, CLK);
  RAM #(.addrWidth(4), .dataWidth(4), .bus("separate")) ram_1 (
    .addr(Address), .din(Write_Data), .data(Data_Read), .str(MemWrite), .clk(not_1_out), .ld(MemRead),
    .clr(CLR));  // open: sel
endmodule
