// Logisim project B1_Group1.circ as structural Verilog: 8 circuits, main circuit main
module main (
  input  Clock,
  input  Reset,
  output [3:0] t0,
  output [3:0] t1,
  output [3:0] t2,
  output [3:0] t3,
  output [3:0] t4,
  output [7:0] PC
);

  MIPS mips_1 (.Clock(Clock), .Reset(Reset), .t0(t0), .t1(t1), .t2(t2), .t3(t3), .t4(t4), .PC(PC));
endmodule

module Registers (
  input  RegWrite,
  input  CLK,
  input  [3:0] Dst_Reg_1,
  input  [3:0] WriteData,
  input  CLR,
  input  [3:0] SrcReg1,
  input  [3:0] SrcReg2,
  output [19:0] t4__t3__t2__t1__t0,
  output [3:0] Read_Data_1,
  output [3:0] Read_Data_2
);

  wire and_1_out, demultiplexer_1_out1, demultiplexer_1_out2, demultiplexer_1_out3, demultiplexer_1_out4,
       demultiplexer_1_out5, demultiplexer_1_out6;
  wire [3:0] sp_q;

  and and_1 (and_1_out, RegWrite, CLK);
  Register #(.width(4), .trigger("falling")) t0 (
    .D(WriteData), .Q(t4__t3__t2__t1__t0[3:0]), .clk(demultiplexer_1_out1), .clr(CLR));  // open: en
  Demultiplexer #(.select(3), .enable("false")) demultiplexer_1 (
    .out1(demultiplexer_1_out1), .out2(demultiplexer_1_out2), .out3(demultiplexer_1_out3),
    .out4(demultiplexer_1_out4), .out5(demultiplexer_1_out5), .out6(demultiplexer_1_out6), .in(and_1_out),
    .sel(Dst_Reg_1[2:0]));  // open: out0, out7
  Register #(.width(4), .trigger("falling")) t1 (
    .D(WriteData), .Q(t4__t3__t2__t1__t0[7:4]), .clk(demultiplexer_1_out2), .clr(CLR));  // open: en
  Register #(.width(4), .trigger("falling")) t2 (
    .D(WriteData), .Q(t4__t3__t2__t1__t0[11:8]), .clk(demultiplexer_1_out3), .clr(CLR));  // open: en
  Register #(.width(4), .trigger("falling")) t3 (
    .D(WriteData), .Q(t4__t3__t2__t1__t0[15:12]), .clk(demultiplexer_1_out4), .clr(CLR));  // open: en
  Register #(.width(4), .trigger("falling")) t4 (
    .D(WriteData), .Q(t4__t3__t2__t1__t0[19:16]), .clk(demultiplexer_1_out5), .clr(CLR));  // open: en
  Register #(.width(4), .trigger("falling")) sp (
    .D(WriteData), .Q(sp_q), .clk(demultiplexer_1_out6), .clr(CLR));  // open: en
  Multiplexer #(.select(3), .width(4), .enable("false")) multiplexer_1 (
    .in0(4'b0000), .in1(t4__t3__t2__t1__t0[3:0]), .in2(t4__t3__t2__t1__t0[7:4]),
    .in3(t4__t3__t2__t1__t0[11:8]), .in4(t4__t3__t2__t1__t0[15:12]), .in5(t4__t3__t2__t1__t0[19:16]),
    .in6(sp_q), .out(Read_Data_1), .sel(SrcReg1[2:0]));  // open: in7
  Multiplexer #(.select(3), .width(4), .enable("false")) multiplexer_2 (
    .in0(4'b0000), .in1(t4__t3__t2__t1__t0[3:0]), .in2(t4__t3__t2__t1__t0[7:4]),
    .in3(t4__t3__t2__t1__t0[11:8]), .in4(t4__t3__t2__t1__t0[15:12]), .in5(t4__t3__t2__t1__t0[19:16]),
    .in6(sp_q), .out(Read_Data_2), .sel(SrcReg2[2:0]));  // open: in7

  // Notes on the sheet:
  //   $zero
endmodule

module Instruction (
  input  [7:0] Read_Address,
  output [3:0] _12_15,
  output [3:0] _8_11,
  output [3:0] _4_7,
  output [3:0] _0_3,
  output [7:0] _0_7
);

  ROM #(.dataWidth(16)) rom_1 (.addr(Read_Address), .data({_12_15, _8_11, _0_7[3:0], _0_3}), .sel(1'b1));

  assign _0_7[7:4] = _0_3;
  assign _4_7 = _0_7[3:0];

  // Notes on the sheet:
  //   contents of rom_1 (hex, n*v repeats v):
  //   7025 7034 f234 50 6235 c231 3232 5242 b313 5343 9443 1241 d356 9331 b252 2221 a331 4727 9421 3115
  //   2661 d620 241 2661 d610 a1c0 8271 a110
endmodule

module Data_Memory (
  input  [3:0] Address,
  input  [3:0] Write_Data,
  input  MemWrite,
  input  MemRead,
  input  CLK,
  input  CLR,
  output [3:0] Data_Read
);

  wire not_1_out;

  not not_1 (not_1_out, CLK);
  RAM #(.addrWidth(4), .dataWidth(4), .bus("separate")) ram_1 (
    .addr(Address), .din(Write_Data), .data(Data_Read), .str(MemWrite), .clk(not_1_out), .ld(MemRead),
    .clr(CLR));  // open: sel
endmodule

module ALU (
  input  [2:0] ALUOp,
  input  [3:0] A,
  input  [3:0] B,
  output [3:0] Output,
  output Zero_flag
);

  wire [3:0] adder_1_out, and_1_out, nor_1_out, or_1_out, shifter_1_out, shifter_2_out, subtractor_1_out;

  Adder #(.width(4)) adder_1 (.a(A), .b(B), .out(adder_1_out), .cin(1'b0));  // open: cout
  Subtractor #(.width(4)) subtractor_1 (.a(A), .b(B), .out(subtractor_1_out), .bin(1'b0));  // open: bout
  assign and_1_out = A & B;  // AND_Gate and_1, 4 bits wide
  assign or_1_out = A | B;  // OR_Gate or_1, 4 bits wide
  assign nor_1_out = ~(A | B);  // NOR_Gate nor_1, 4 bits wide
  Shifter #(.width(4)) shifter_1 (.in(A), .\dist (B[1:0]), .out(shifter_1_out));
  Shifter #(.width(4), .shift("lr")) shifter_2 (.in(A), .\dist (B[1:0]), .out(shifter_2_out));
  Multiplexer #(.select(3), .width(4), .enable("false")) multiplexer_1 (
    .in0(adder_1_out), .in1(subtractor_1_out), .in2(and_1_out), .in3(or_1_out), .in4(nor_1_out),
    .in5(shifter_1_out), .in6(shifter_2_out), .in7(4'b0000), .out(Output), .sel(ALUOp));
  nor nor_2 (Zero_flag, Output[0], Output[1], Output[2], Output[3]);
endmodule

module Control (
  input  [3:0] OP_Code,
  output [2:0] ALUOp,
  output Jump,
  output bneq,
  output beq,
  output MemWrite,
  output MemRead,
  output RegWrite,
  output MemToReg,
  output ALUSrc,
  output RegDst
);

  ROM #(.addrWidth(4), .dataWidth(12)) rom_1 (
    .addr(OP_Code), .data({RegDst, ALUSrc, MemToReg, RegWrite, MemRead, MemWrite, beq, bneq, Jump, ALUOp}));  // open: sel

  // Notes on the sheet:
  //   contents of rom_1 (hex, n*v repeats v):
  //   8 903 505 11 904 640 901 500 503 501 506 780 21 502 902 900
endmodule

module MIPS (
  input  Clock,
  input  Reset,
  output [7:0] PC,
  output [3:0] t0,
  output [3:0] t1,
  output [3:0] t2,
  output [3:0] t3,
  output [3:0] t4
);

  wire alu_1_zero_flag, control_1_alusrc, control_1_beq, control_1_bneq, control_1_jump, control_1_memread,
       control_1_memtoreg, control_1_memwrite, control_1_regdst, control_1_regwrite, multiplexer_2_out;
  wire [2:0] control_1_aluop;
  wire [3:0] alu_1_output, data_memory_1_data_read, instruction_1__0_3, instruction_1__4_7,
       instruction_1__8_11, instruction_1__12_15, multiplexer_1_out, multiplexer_3_out, multiplexer_6_out,
       registers_1_read_data_1, registers_1_read_data_2;
  wire [7:0] adder_1_out, adder_2_out, bit_extender_1_out, instruction_1__0_7, multiplexer_4_out,
       multiplexer_5_out;

  Register #(.trigger("falling")) register_1 (.D(multiplexer_5_out), .Q(PC), .clk(Clock), .clr(Reset));  // open: en
  Adder adder_1 (.a(PC), .b(8'h1), .out(adder_1_out));  // open: cin, cout
  Instruction instruction_1 (
    .Read_Address(PC), ._12_15(instruction_1__12_15), ._8_11(instruction_1__8_11), ._4_7(instruction_1__4_7),
    ._0_3(instruction_1__0_3), ._0_7(instruction_1__0_7));
  // Probe on instruction_1__8_11
  // Probe on instruction_1__4_7
  // Probe on instruction_1__0_3
  assign bit_extender_1_out = {{4{1'b0}}, instruction_1__0_3};  // Bit_Extender bit_extender_1
  // Probe on multiplexer_1_out
  Multiplexer #(.width(4), .enable("false")) multiplexer_1 (
    .in0(instruction_1__4_7), .in1(instruction_1__0_3), .out(multiplexer_1_out), .sel(control_1_regdst));
  Control control_1 (
    .OP_Code(instruction_1__12_15), .ALUOp(control_1_aluop), .Jump(control_1_jump), .bneq(control_1_bneq),
    .beq(control_1_beq), .MemWrite(control_1_memwrite), .MemRead(control_1_memread),
    .RegWrite(control_1_regwrite), .MemToReg(control_1_memtoreg), .ALUSrc(control_1_alusrc),
    .RegDst(control_1_regdst));
  Adder adder_2 (.a(bit_extender_1_out), .b(adder_1_out), .out(adder_2_out));  // open: cin, cout
  // Probe on registers_1_read_data_1
  Registers registers_1 (
    .Dst_Reg_1(multiplexer_1_out), .WriteData(multiplexer_6_out), .SrcReg2(instruction_1__4_7),
    .RegWrite(control_1_regwrite), .CLK(Clock), .Read_Data_2(registers_1_read_data_2), .CLR(Reset),
    .t4__t3__t2__t1__t0({t4, t3, t2, t1, t0}), .Read_Data_1(registers_1_read_data_1),
    .SrcReg1(instruction_1__8_11));
  Multiplexer #(.enable("false")) multiplexer_2 (
    .in0(control_1_bneq), .in1(control_1_beq), .out(multiplexer_2_out), .sel(alu_1_zero_flag));
  Multiplexer #(.width(4), .enable("false")) multiplexer_3 (
    .in0(registers_1_read_data_2), .in1(instruction_1__0_3), .out(multiplexer_3_out), .sel(control_1_alusrc));
  Multiplexer #(.width(8), .enable("false")) multiplexer_4 (
    .in0(adder_1_out), .in1(adder_2_out), .out(multiplexer_4_out), .sel(multiplexer_2_out));
  // Probe on multiplexer_3_out
  ALU alu_1 (
    .ALUOp(control_1_aluop), .A(registers_1_read_data_1), .B(multiplexer_3_out), .Output(alu_1_output),
    .Zero_flag(alu_1_zero_flag));
  Multiplexer #(.width(8), .enable("false")) multiplexer_5 (
    .in0(multiplexer_4_out), .in1(instruction_1__0_7), .out(multiplexer_5_out), .sel(control_1_jump));
  // Probe on alu_1_output
  // Probe on registers_1_read_data_2
  Data_Memory data_memory_1 (
    .Address(alu_1_output), .Write_Data(registers_1_read_data_2), .CLK(Clock),
    .Data_Read(data_memory_1_data_read), .MemRead(control_1_memread), .MemWrite(control_1_memwrite),
    .CLR(Reset));
  Multiplexer #(.width(4), .enable("false")) multiplexer_6 (
    .in0(alu_1_output), .in1(data_memory_1_data_read), .out(multiplexer_6_out), .sel(control_1_memtoreg));
  // Probe on multiplexer_6_out
endmodule

module Main_2 (
  input  in_1,
  output [3:0] t0,
  output [3:0] t1,
  output [3:0] t2,
  output [3:0] t3,
  output [3:0] t4
);

  wire alu_1_zero_flag, clock_1_out, control_1_alusrc, control_1_beq, control_1_bneq, control_1_jump,
       control_1_memread, control_1_memtoreg, control_1_memwrite, control_1_regdst, control_1_regwrite,
       multiplexer_2_out;
  wire [2:0] control_1_aluop;
  wire [3:0] alu_1_output, data_memory_1_data_read, instruction_1__0_3, instruction_1__4_7,
       instruction_1__8_11, instruction_1__12_15, multiplexer_1_out, multiplexer_3_out, multiplexer_6_out,
       registers_1_read_data_1, registers_1_read_data_2;
  wire [7:0] adder_1_out, adder_2_out, bit_extender_1_out, instruction_1__0_7, multiplexer_4_out,
       multiplexer_5_out, register_1_q;

  Clock clock_1 (.out(clock_1_out));
  Register #(.trigger("falling")) register_1 (
    .D(multiplexer_5_out), .Q(register_1_q), .clk(clock_1_out), .clr(in_1));  // open: en
  Adder adder_1 (.a(register_1_q), .b(8'h1), .out(adder_1_out));  // open: cin, cout
  Instruction instruction_1 (
    .Read_Address(register_1_q), ._12_15(instruction_1__12_15), ._8_11(instruction_1__8_11),
    ._4_7(instruction_1__4_7), ._0_3(instruction_1__0_3), ._0_7(instruction_1__0_7));
  // Probe on instruction_1__8_11
  // Probe on instruction_1__4_7
  // Probe on instruction_1__0_3
  assign bit_extender_1_out = {{4{1'b0}}, instruction_1__0_3};  // Bit_Extender bit_extender_1
  // Probe on multiplexer_1_out
  Multiplexer #(.width(4), .enable("false")) multiplexer_1 (
    .in0(instruction_1__4_7), .in1(instruction_1__0_3), .out(multiplexer_1_out), .sel(control_1_regdst));
  Control control_1 (
    .OP_Code(instruction_1__12_15), .ALUOp(control_1_aluop), .Jump(control_1_jump), .bneq(control_1_bneq),
    .beq(control_1_beq), .MemWrite(control_1_memwrite), .MemRead(control_1_memread),
    .RegWrite(control_1_regwrite), .MemToReg(control_1_memtoreg), .ALUSrc(control_1_alusrc),
    .RegDst(control_1_regdst));
  Adder adder_2 (.a(bit_extender_1_out), .b(adder_1_out), .out(adder_2_out));  // open: cin, cout
  // Probe on registers_1_read_data_1
  Registers registers_1 (
    .Dst_Reg_1(multiplexer_1_out), .WriteData(multiplexer_6_out), .SrcReg2(instruction_1__4_7),
    .RegWrite(control_1_regwrite), .CLK(clock_1_out), .Read_Data_2(registers_1_read_data_2), .CLR(in_1),
    .t4__t3__t2__t1__t0({t4, t3, t2, t1, t0}), .Read_Data_1(registers_1_read_data_1),
    .SrcReg1(instruction_1__8_11));
  Multiplexer #(.enable("false")) multiplexer_2 (
    .in0(control_1_bneq), .in1(control_1_beq), .out(multiplexer_2_out), .sel(alu_1_zero_flag));
  Multiplexer #(.width(4), .enable("false")) multiplexer_3 (
    .in0(registers_1_read_data_2), .in1(instruction_1__0_3), .out(multiplexer_3_out), .sel(control_1_alusrc));
  Multiplexer #(.width(8), .enable("false")) multiplexer_4 (
    .in0(adder_1_out), .in1(adder_2_out), .out(multiplexer_4_out), .sel(multiplexer_2_out));
  // Probe on multiplexer_3_out
  ALU alu_1 (
    .ALUOp(control_1_aluop), .A(registers_1_read_data_1), .B(multiplexer_3_out), .Output(alu_1_output),
    .Zero_flag(alu_1_zero_flag));
  Multiplexer #(.width(8), .enable("false")) multiplexer_5 (
    .in0(multiplexer_4_out), .in1(instruction_1__0_7), .out(multiplexer_5_out), .sel(control_1_jump));
  // Probe on alu_1_output
  // Probe on registers_1_read_data_2
  Data_Memory data_memory_1 (
    .Address(alu_1_output), .Write_Data(registers_1_read_data_2), .CLK(clock_1_out),
    .Data_Read(data_memory_1_data_read), .MemRead(control_1_memread), .MemWrite(control_1_memwrite),
    .CLR(in_1));
  Multiplexer #(.width(4), .enable("false")) multiplexer_6 (
    .in0(alu_1_output), .in1(data_memory_1_data_read), .out(multiplexer_6_out), .sel(control_1_memtoreg));
  // Probe on multiplexer_6_out
endmodule
