// Logisim project 4bit-ALU.circ as structural Verilog
module logic_unit (
  input  Ao,
  input  A1,
  input  A2,
  input  A3,
  input  Bo,
  input  B1,
  input  B2,
  input  B3
);

  wire arithmetic_unit_1_p1, arithmetic_unit_1_p2, arithmetic_unit_1_p3, n7404_1_p6, n7404_1_p8, n7404_1_p10,
       n7404_1_p12, n7404_1_p13, n7408_1_p13, n7408_1_p14, n74157_1_p3, n74157_1_p6, n74157_1_p7,
       n74157_1_p9, n74157_1_p10, n74157_1_p12, n74157_2_p3, n74157_2_p6, n74157_2_p9, n74157_2_p12;

  // _7404 7404_1: pin names not known; wires that end beside it: Bo, B1, B2, B3, Ao, n7404_1_p6, A1, n7404_1_p8, A3, n7404_1_p10, A2, n7404_1_p12, n7404_1_p13
  // _7408 7408_1: pin names not known; wires that end beside it: Bo, B1, B2, B3, Ao, Bo, A1, B1, A2, B2, A3, B3, n7408_1_p13, n7408_1_p14
  // arithmetic_unit arithmetic_unit_1: pin names not known; wires that end beside it: arithmetic_unit_1_p1, arithmetic_unit_1_p2, arithmetic_unit_1_p3
  // _74157 74157_1: pin names not known; wires that end beside it: n7408_1_p14, n7404_1_p6, n74157_1_p3, n7408_1_p13, n7404_1_p8, n74157_1_p6, n74157_1_p7, n7404_1_p10, n74157_1_p9, n74157_1_p10, n7404_1_p12, n74157_1_p12, n74157_1_p7, n74157_1_p10
  // _74157 74157_2: pin names not known; wires that end beside it: arithmetic_unit_1_p1, n74157_1_p3, n74157_2_p3, n74157_1_p6, arithmetic_unit_1_p2, n74157_2_p6, n74157_1_p9, n7404_1_p13, n74157_2_p9, n74157_1_p12, arithmetic_unit_1_p3, n74157_2_p12, n74157_2_p3, n74157_2_p6, n74157_2_p9, n74157_2_p12
endmodule

module arithmetic_unit (
  input  in_1,
  input  in_2,
  input  in_3,
  input  in_4,
  input  in_5,
  input  in_6,
  input  in_7,
  input  in_8,
  input  CS2,
  input  CS1,
  input  CS0
);

  wire n7404_1_p8, n7404_1_p10, n7404_1_p12, n7404_2_p2, n7404_2_p4, n7404_2_p6, n7404_2_p8, n7432_1_p1,
       n7432_1_p3, n7432_1_p6, n7432_1_p8, n7432_1_p9, n7432_1_p10, n7432_2_p1, n7432_2_p2, n7432_2_p4,
       n7432_2_p5, n7432_2_p10, n7432_2_p11, n7432_2_p12, n7483_1_p1, n7483_1_p2, n7483_1_p3, n7483_1_p4,
       n74138_1_p4, n74138_1_p5, n74138_1_p14, n74138_1_p15, n74138_1_p16, n74138_1_p17, n74138_1_p18,
       n74138_1_p19, n74138_1_p20;

  // _74138 74138_1: pin names not known; wires that end beside it: CS0, CS1, CS2, n74138_1_p4, n74138_1_p5, in_1, in_2, in_3, in_4, in_5, in_6, in_7, in_8, n74138_1_p14, n74138_1_p15, n74138_1_p16, n74138_1_p17, n74138_1_p18, n74138_1_p19, n74138_1_p20
  // _7483 7483_1: pin names not known; wires that end beside it: n7483_1_p1, n7483_1_p2, n7483_1_p3, n7483_1_p4, in_1, in_2, n7483_1_p2, n7483_1_p3, in_3, n7483_1_p1, n74138_1_p5, n7483_1_p4, in_4
  // _7432 7432_1: pin names not known; wires that end beside it: n7432_1_p1, n7432_1_p1, n7432_1_p3, n7483_1_p3, n7432_1_p1, n7432_1_p6, n7483_1_p2, n7432_1_p8, n7432_1_p9, n7432_1_p10, n7432_1_p10, n7432_1_p1, n7483_1_p4, n7432_1_p1
  // _7404 7404_1: pin names not known; wires that end beside it: n74138_1_p14, n74138_1_p17, n74138_1_p18, n74138_1_p19, n74138_1_p15, n7432_1_p1, n74138_1_p16, n7404_1_p8, n74138_1_p20, n7404_1_p10, n74138_1_p4, n7404_1_p12, n7404_1_p12, n7432_1_p1
  or or_1 (n7483_1_p1, n7432_1_p1, n7432_2_p12);
  // _7432 7432_2: pin names not known; wires that end beside it: n7432_2_p1, n7432_2_p2, n7432_1_p6, n7432_2_p4, n7432_2_p5, n7432_1_p3, n7404_1_p10, n7404_1_p8, n74138_1_p5, n7432_2_p10, n7432_2_p11, n7432_2_p12
  // _7408 7408_1: pin names not known; wires that end beside it: in_5, n7404_1_p12, n7432_2_p10, in_6, n7404_1_p12, n7432_2_p1, in_7, n7404_1_p12, n7432_2_p4, in_8, n7404_1_p12, n7432_1_p8
  // _7404 7404_2: pin names not known; wires that end beside it: in_8, n7404_2_p2, in_7, n7404_2_p4, in_6, n7404_2_p6, in_5, n7404_2_p8, in_1, in_2, in_3, in_4
  // _7408 7408_2: pin names not known; wires that end beside it: n7404_2_p2, n74138_1_p5, n7432_1_p9, n7404_2_p4, n74138_1_p5, n7432_2_p5, n7404_2_p6, n74138_1_p5, n7432_2_p2, n7404_2_p8, n74138_1_p5, n7432_2_p11, n7404_2_p4, n7404_2_p6, n7404_2_p8, n7404_1_p12, n74138_1_p5, n7483_1_p1, n7483_1_p2, n7483_1_p3, n7483_1_p4

  // Notes on the sheet:
  //   DECODER
  //   CS1*CS0'
  //   Y3
  //   A3
  //   A2
  //   A1
  //   A0
  //   B3
  //   B2
  //   B1
  //   B0
  //   001
  //   001
  //   010
  //   110
  //   111
  //   CS2*CS1*CS0*Bi
  //   B0'
  //   B1'
  //   B2'
  //   B3'
endmodule

module \logic  (
  input  CS2,
  input  CS1,
  input  CS0,
  input  A2,
  input  A1,
  input  A0,
  input  in_7,
  input  B3,
  input  B2,
  input  B1,
  input  B0,
  output C,
  output V,
  output Z,
  output S,
  output F3,
  output F1,
  output F0,
  output out_19
);

  wire adder_1_s0, adder_1_s1, adder_1_s2, adder_1_s3, decoder_1__000, decoder_1__001, decoder_1__010,
       decoder_1__011, decoder_1__110, decoder_1__111, n7404_1_p2, n7404_1_p4, n7404_1_p8, n7404_1_p10,
       n7404_2_p2, n7404_2_p4, n7404_2_p6, n7404_2_p8, n7432_1_p3, n7432_1_p5, n7432_1_p6, n7432_2_p3,
       n7432_2_p4, n7432_2_p6, n7432_3_p2, n7432_3_p3, n7432_3_p5, n7432_3_p6, n7432_3_p7, n7432_3_p8,
       n7432_3_p9, n7432_3_p12, n7432_4_p1, n7432_4_p2, n7432_4_p4, n7432_4_p5, n7432_4_p9, n7432_4_p10,
       n7432_4_p11, n7486_1_p2, n74157_1_p3, n74157_1_p4, n74157_1_p6, n74157_1_p7, n74157_1_p10,
       n74157_1_p11, n74157_1_p13, n74157_1_p14;

  // _7432 7432_1: pin names not known; wires that end beside it: out_19, F0, n7432_1_p3, n7432_1_p3, n7432_1_p5, n7432_1_p6, F3, F1, n7432_1_p5
  Decoder decoder_1 (
    .in_1(CS2), .in_2(CS1), .in_3(CS0), ._000(decoder_1__000), ._001(decoder_1__001), ._010(decoder_1__010),
    ._011(decoder_1__011), ._110(decoder_1__110), ._111(decoder_1__111));  // open: _100, _101
  // _7486 7486_1: pin names not known; wires that end beside it: C, n7486_1_p2, V
  // _7432 7432_2: pin names not known; wires that end beside it: decoder_1__011, decoder_1__000, n7432_2_p3, n7432_2_p4, decoder_1__001, n7432_2_p6
  Adder adder_1 (
    .B3(n7432_2_p6), .B2(n7432_3_p6), .B1(n7432_3_p3), .B0(n7432_3_p12), .A3(A2), .A2(A1), .A1(A0),
    .A0(in_7), .C4(C), .S3(adder_1_s3), .C3(n7486_1_p2), .S2(adder_1_s2), .S1(adder_1_s1), .S0(adder_1_s0),
    .Cin(n7432_4_p9));  // open: C2, C1
  // _7432 7432_3: pin names not known; wires that end beside it: decoder_1__001, n7432_3_p2, n7432_3_p3, decoder_1__001, n7432_3_p5, n7432_3_p6, n7432_3_p7, n7432_3_p8, n7432_3_p9, n7432_3_p9, decoder_1__001, n7432_3_p12, decoder_1__001, n7432_2_p6, n7432_3_p6, n7432_3_p3, n7432_3_p12
  // _7404 7404_1: pin names not known; wires that end beside it: in_7, n7404_1_p2, A0, n7404_1_p4, n7432_1_p6, Z, A1, n7404_1_p8, A2, n7404_1_p10, A2, A1, A0, in_7
  // _74157 74157_1: pin names not known; wires that end beside it: decoder_1__000, n7404_1_p2, n74157_1_p3, n74157_1_p4, n7404_1_p4, n74157_1_p6, n74157_1_p7, 1'b0, n7404_1_p8, n74157_1_p10, n74157_1_p11, n7404_1_p10, n74157_1_p13, n74157_1_p14
  // _7408 7408_1: pin names not known; wires that end beside it: in_7, B0, n74157_1_p3, A0, B1, n74157_1_p6, A1, B2, n74157_1_p10, A2, B3, n74157_1_p13, in_7, A0, A1, A2, B0, B1, B2, B3
  // _7432 7432_4: pin names not known; wires that end beside it: n7432_4_p1, n7432_4_p2, n7432_3_p5, n7432_4_p4, n7432_4_p5, n7432_3_p2, decoder_1__110, decoder_1__010, n7432_4_p9, n7432_4_p10, n7432_4_p11, n7432_2_p4
  // _74157 74157_2: pin names not known; wires that end beside it: n7432_2_p3, adder_1_s0, n74157_1_p4, out_19, adder_1_s1, n74157_1_p7, F0, 1'b0, adder_1_s2, n74157_1_p11, F1, adder_1_s3, n74157_1_p14, F3
  // _7408 7408_2: pin names not known; wires that end beside it: B3, decoder_1__111, n7432_4_p10, B2, decoder_1__111, n7432_4_p1, B1, decoder_1__111, n7432_4_p4, B0, decoder_1__111, n7432_3_p7
  // _7404 7404_2: pin names not known; wires that end beside it: B0, n7404_2_p2, B1, n7404_2_p4, B2, n7404_2_p6, B3, n7404_2_p8, B3, B2, B1, B0
  // _7408 7408_3: pin names not known; wires that end beside it: n7404_2_p2, n7432_4_p9, n7432_3_p8, n7404_2_p4, n7432_4_p9, n7432_4_p5, n7404_2_p6, n7432_4_p9, n7432_4_p2, n7404_2_p8, n7432_4_p9, n7432_4_p11, decoder_1__111, n7432_4_p9

  assign S = F3;

  // Notes on the sheet:
  //   NOR FOR ZF
  //   XOR FOR OF
  //   A3
  //   F2
  //   CS1*CS0'
  //   001
  //   010
  //   110
  //   111
  //   CS2*CS1*CS0*Bi
  //   B1'
  //   B0'
  //   B2'
  //   B3'
  //   B3
  //   B2
  //   B1
  //   B0
endmodule

module Decoder (
  input  in_1,
  input  in_2,
  input  in_3,
  output _000,
  output _001,
  output _010,
  output _011,
  output _100,
  output _101,
  output _110,
  output _111
);

  wire n74138_1_p7, n74138_1_p10, n74138_1_p11, n74138_1_p12, n74138_1_p13, n74138_1_p14;

  // _74138 74138_1: pin names not known; wires that end beside it: in_3, in_2, in_1, 1'b0, 1'b0, 1'b1, n74138_1_p7, 1'b0, 1'b1, n74138_1_p10, n74138_1_p11, n74138_1_p12, n74138_1_p13, n74138_1_p14
  // _7404 7404_1: pin names not known; wires that end beside it: n74138_1_p11, _001, n74138_1_p12, _010, n74138_1_p13, _011, 1'b0, 1'b1, n74138_1_p10, _000, n74138_1_p7, _111, n74138_1_p14, _110, _100, _101

  // Notes on the sheet:
  //   3x8 DECODER
endmodule

module Adder (
  input  B3,
  input  B2,
  input  B1,
  input  B0,
  input  A3,
  input  A2,
  input  A1,
  input  A0,
  input  Cin,
  output S3,
  output S2,
  output S1,
  output S0,
  output C4,
  output C3,
  output C2,
  output C1
);

  // _7483 7483_1: pin names not known; wires that end beside it: A1, C1, C1, 1'b1, C1, 1'b0, 1'b0, B1, S1, C2, Cin, 1'b0, B0, A0, S0
  // _7483 7483_2: pin names not known; wires that end beside it: A3, C3, C3, 1'b1, C3, 1'b0, 1'b0, B3, S3, C4, C2, 1'b0, B2, A2, S2
endmodule
