// Logisim project combinational_part.circ as structural Verilog: 1 circuit, main circuit main
module main (
  input  in_1,
  input  in_2,
  input  in_3,
  input  in_4,
  input  in_5,
  input  in_6,
  input  in_7,
  input  in_8,
  input  CS2,
  input  CS1,
  input  CS0
);

  wire n7404_1_p8, n7404_1_p10, n7404_1_p12, n7404_2_p2, n7404_2_p4, n7404_2_p6, n7404_2_p8, n7432_1_p1,
       n7432_1_p3, n7432_1_p6, n7432_1_p8, n7432_1_p9, n7432_1_p10, n7432_2_p1, n7432_2_p2, n7432_2_p4,
       n7432_2_p5, n7432_2_p10, n7432_2_p11, n7432_2_p12, n7483_1_p1, n7483_1_p2, n7483_1_p3, n7483_1_p4,
       n74138_1_p4, n74138_1_p5, n74138_1_p14, n74138_1_p15, n74138_1_p16, n74138_1_p17, n74138_1_p18,
       n74138_1_p19, n74138_1_p20;

  // _74138 74138_1: pin names not known; wires that end beside it: CS0, CS1, CS2, n74138_1_p4, n74138_1_p5, in_1, in_2, in_3, in_4, in_5, in_6, in_7, in_8, n74138_1_p14, n74138_1_p15, n74138_1_p16, n74138_1_p17, n74138_1_p18, n74138_1_p19, n74138_1_p20
  // _7483 7483_1: pin names not known; wires that end beside it: n7483_1_p1, n7483_1_p2, n7483_1_p3, n7483_1_p4, in_1, in_2, n7483_1_p2, n7483_1_p3, in_3, n7483_1_p1, n74138_1_p5, n7483_1_p4, in_4
  // _7432 7432_1: pin names not known; wires that end beside it: n7432_1_p1, n7432_1_p1, n7432_1_p3, n7483_1_p3, n7432_1_p1, n7432_1_p6, n7483_1_p2, n7432_1_p8, n7432_1_p9, n7432_1_p10, n7432_1_p10, n7432_1_p1, n7483_1_p4, n7432_1_p1
  // _7404 7404_1: pin names not known; wires that end beside it: n74138_1_p14, n74138_1_p17, n74138_1_p18, n74138_1_p19, n74138_1_p15, n7432_1_p1, n74138_1_p16, n7404_1_p8, n74138_1_p20, n7404_1_p10, n74138_1_p4, n7404_1_p12, n7404_1_p12, n7432_1_p1
  or or_1 (n7483_1_p1, n7432_1_p1, n7432_2_p12);
  // _7432 7432_2: pin names not known; wires that end beside it: n7432_2_p1, n7432_2_p2, n7432_1_p6, n7432_2_p4, n7432_2_p5, n7432_1_p3, n7404_1_p10, n7404_1_p8, n74138_1_p5, n7432_2_p10, n7432_2_p11, n7432_2_p12
  // _7408 7408_1: pin names not known; wires that end beside it: in_5, n7404_1_p12, n7432_2_p10, in_6, n7404_1_p12, n7432_2_p1, in_7, n7404_1_p12, n7432_2_p4, in_8, n7404_1_p12, n7432_1_p8
  // _7404 7404_2: pin names not known; wires that end beside it: in_8, n7404_2_p2, in_7, n7404_2_p4, in_6, n7404_2_p6, in_5, n7404_2_p8, in_1, in_2, in_3, in_4
  // _7408 7408_2: pin names not known; wires that end beside it: n7404_2_p2, n74138_1_p5, n7432_1_p9, n7404_2_p4, n74138_1_p5, n7432_2_p5, n7404_2_p6, n74138_1_p5, n7432_2_p2, n7404_2_p8, n74138_1_p5, n7432_2_p11, n7404_2_p4, n7404_2_p6, n7404_2_p8, n7404_1_p12, n74138_1_p5, n7483_1_p1, n7483_1_p2, n7483_1_p3, n7483_1_p4

  // Notes on the sheet:
  //   DECODER
  //   CS1*CS0'
  //   Y3
  //   A3
  //   A2
  //   A1
  //   A0
  //   B3
  //   B2
  //   B1
  //   B0
  //   001
  //   001
  //   010
  //   110
  //   111
  //   CS2*CS1*CS0*Bi
  //   B0'
  //   B1'
  //   B2'
  //   B3'
endmodule
